// Logisim project thijs 22-23.circ as structural Verilog: 7 circuits, main circuit main
module main (
  input  reset,
  output [8:0] out_2
);

  wire clock_out;
  wire [2:0] decoder_1_func_code, decoder_1_op_code, decoder_1_rs, decoder_1_rt;
  wire [7:0] decoder_1_off_addr, pc_1_instructie_address;

  Clock clock (.out(clock_out));
  decoder decoder_1 (
    .in_1(out_2), .Func_Code(decoder_1_func_code), .OP_CODE(decoder_1_op_code), .Rs(decoder_1_rs),
    .Rt(decoder_1_rt), .off_addr(decoder_1_off_addr));
  PC pc_1 (
    .Offset(decoder_1_off_addr), .clock(clock_out), .reset(reset),
    .Instructie_address(pc_1_instructie_address));  // open: absolute, relative
  controller controller_1 ();  // open: OP_Code, Func_Code
  RAM #(.dataWidth(9)) ram_1 (.addr(pc_1_instructie_address), .data(out_2));  // open: sel, clk, ld, clr
  registers registers_1 (
    .Rs(decoder_1_rs), .Rt(decoder_1_rt), .Rd(decoder_1_rs), .reset(reset), .clock(clock_out));  // open: write_register, DATA, Rs_2, Rt_2, AP
  RAM ram_2 (.clk(clock_out));  // open: addr, data, sel, ld, clr
endmodule

module PC (
  input  absolute,
  input  relative,
  input  [7:0] Offset,
  input  clock,
  input  reset,
  output [7:0] Instructie_address
);

  wire not_1_out, or_1_out;
  wire [7:0] adder_1_out, adder_2_out, multiplexer_1_out;

  Adder adder_1 (.a(Instructie_address), .b(8'h1), .out(adder_1_out));  // open: cin, cout
  Adder adder_2 (.a(adder_1_out), .b(Offset), .out(adder_2_out));  // open: cin, cout
  or or_1 (or_1_out, relative, absolute);
  Multiplexer #(.width(8), .enable("false")) multiplexer_1 (
    .in0(Offset), .in1(adder_2_out), .out(multiplexer_1_out), .sel(relative));
  not not_1 (not_1_out, or_1_out);
  Counter counter_1 (
    .load(or_1_out), .D(multiplexer_1_out), .count(not_1_out), .Q(Instructie_address), .clk(clock),
    .clr(reset));  // open: carry
endmodule

module decoder (
  input  [8:0] in_1,
  output [2:0] Func_Code,
  output [2:0] OP_CODE,
  output [2:0] Rs,
  output [2:0] Rt,
  output [7:0] off_addr
);


  assign Func_Code = in_1[2:0];
  assign off_addr = {{3{in_1[5]}}, in_1[4:0]};
  assign OP_CODE = in_1[8:6];
  assign Rs = in_1[5:3];
  assign Rt = in_1[2:0];
endmodule

// control
module controller (
  input  [2:0] OP_Code,
  input  [2:0] Func_Code
);
endmodule

module alu (
  input  [1:0] in_1,
  input  [7:0] A,
  input  [7:0] B,
  output [7:0] \output 
);

  wire [7:0] adder_1_out, not_1_out, or_1_out, subtractor_1_out;

  assign or_1_out = A | B;  // OR_Gate or_1, 8 bits wide
  Adder adder_1 (.a(A), .b(B), .out(adder_1_out));  // open: cin, cout
  Subtractor subtractor_1 (.a(A), .b(B), .out(subtractor_1_out));  // open: bin, bout
  assign not_1_out = ~A;  // NOT_Gate not_1, 8 bits wide
  Multiplexer #(.select(2), .width(8)) multiplexer_1 (
    .in0(or_1_out), .in1(adder_1_out), .in2(subtractor_1_out), .in3(not_1_out), .out(\output ), .sel(in_1));  // open: en
endmodule

// reg
module registers (
  input  write_register,
  input  [2:0] Rs,
  input  [2:0] Rt,
  input  [2:0] Rd,
  input  [7:0] DATA,
  input  reset,
  input  clock,
  output [7:0] Rs_2,
  output [7:0] Rt_2,
  output [7:0] AP
);

  wire demultiplexer_1_out0, demultiplexer_1_out1, demultiplexer_1_out2, demultiplexer_1_out3,
       demultiplexer_1_out4, demultiplexer_1_out5, demultiplexer_1_out6, demultiplexer_1_out7;
  wire [7:0] register_1_q, register_2_q, register_3_q, register_4_q, register_5_q, register_6_q, register_7_q;

  Demultiplexer #(.select(3), .enable("false")) demultiplexer_1 (
    .out0(demultiplexer_1_out0), .out1(demultiplexer_1_out1), .out2(demultiplexer_1_out2),
    .out3(demultiplexer_1_out3), .out4(demultiplexer_1_out4), .out5(demultiplexer_1_out5),
    .out6(demultiplexer_1_out6), .out7(demultiplexer_1_out7), .in(write_register), .sel(Rd));
  Register register_1 (.D(DATA), .en(demultiplexer_1_out0), .Q(register_1_q), .clk(clock), .clr(reset));
  Register register_2 (.D(DATA), .en(demultiplexer_1_out1), .Q(register_2_q), .clk(clock), .clr(reset));
  Register register_3 (.D(DATA), .en(demultiplexer_1_out2), .Q(register_3_q), .clk(clock), .clr(reset));
  Register register_4 (.D(DATA), .en(demultiplexer_1_out3), .Q(register_4_q), .clk(clock), .clr(reset));
  Register register_5 (.D(DATA), .en(demultiplexer_1_out4), .Q(register_5_q), .clk(clock), .clr(reset));
  Register register_6 (.D(DATA), .en(demultiplexer_1_out5), .Q(register_6_q), .clk(clock), .clr(reset));
  Register register_7 (.D(DATA), .en(demultiplexer_1_out6), .Q(register_7_q), .clk(clock), .clr(reset));
  Register register_8 (.D(DATA), .en(demultiplexer_1_out7), .Q(AP), .clk(clock), .clr(reset));
  Multiplexer #(.select(3), .width(8), .enable("false")) multiplexer_1 (
    .in0(register_1_q), .in1(register_2_q), .in2(register_3_q), .in3(register_4_q), .in4(register_5_q),
    .in5(register_6_q), .in6(register_7_q), .in7(AP), .out(Rs_2));  // open: sel
  Multiplexer #(.select(3), .width(8), .enable("false")) multiplexer_2 (
    .in0(register_1_q), .in1(register_2_q), .in2(register_3_q), .in3(register_4_q), .in4(register_5_q),
    .in5(register_6_q), .in6(register_7_q), .in7(AP), .out(Rt_2), .sel(Rt));
endmodule

module stack (
  input  in_1
);

  wire [7:0] adder_1_out, multiplexer_1_out, multiplexer_2_out, register_1_q, subtractor_1_out;

  Adder adder_1 (.a(register_1_q), .b(8'h1), .out(adder_1_out));  // open: cin, cout
  Subtractor subtractor_1 (.a(register_1_q), .b(8'h1), .out(subtractor_1_out));  // open: bin, bout
  Multiplexer #(.width(8), .enable("false")) multiplexer_1 (
    .in0(adder_1_out), .in1(subtractor_1_out), .out(multiplexer_1_out), .sel(in_1));
  Register register_1 (.D(multiplexer_1_out), .Q(register_1_q));  // open: en, clk, clr
  Multiplexer #(.width(8), .enable("false")) multiplexer_2 (
    .in0(register_1_q), .in1(subtractor_1_out), .out(multiplexer_2_out));  // open: sel
  RAM #(.bus("separate")) ram_1 (.addr(multiplexer_2_out));  // open: din, data, str, sel, clk, ld, clr
endmodule
