// Logisim project Examen_templat(kaeyman).circ as structural Verilog
module Controller (
  input  [1:0] Function_Code,
  input  [1:0] Op_Code,
  output Branch,
  output Jump,
  output StackWrite,
  output StackRead,
  output RegistorWrite,
  output RegistorRead,
  output [1:0] ALU,
  output Imm_Address,
  output Increase_SP,
  output Decrease_SP
);

  wire demultiplexer_1_out0, demultiplexer_1_out1, demultiplexer_1_out2, demultiplexer_1_out3,
       demultiplexer_2_out0, demultiplexer_2_out1, demultiplexer_2_out2, demultiplexer_2_out3;

  Demultiplexer #(.select(2), .enable("false")) demultiplexer_1 (
    .out0(demultiplexer_1_out0), .out1(demultiplexer_1_out1), .out2(demultiplexer_1_out2),
    .out3(demultiplexer_1_out3), .in(1'b1), .sel(Function_Code));
  Demultiplexer #(.select(2), .enable("false")) demultiplexer_2 (
    .out0(demultiplexer_2_out0), .out1(demultiplexer_2_out1), .out2(demultiplexer_2_out2),
    .out3(demultiplexer_2_out3), .in(1'b1), .sel(Op_Code));

  // Notes on the sheet:
  //   & meer
endmodule

module Datapad (
  input  C,
  input  R
);


  // Notes on the sheet:
  //   LDI -> LDI r5 2 -> r5 = 2
  //   CLR -> SP = SP - 1
  //   Functionaliteiten: ALU, LDI, POP, PUSH, CLR, JUMP, BRNZ
  //   POP -> POP r1 -> r1 = MEM[SP-1]; SP = SP -1; PC = PC +1
  //   PUSH -> PUSH r1 -> MEM[SP-1] = r1; SP = SP + 1; PC = PC + 1
endmodule

module PC (
  input  Branch,
  input  Jump,
  output Offset,
  output Instructie_address
);


  // Notes on the sheet:
  //   Antwoord: 6 -> 2^6 = 64
  //   Vraag: Is de program counter signed of unsigned? Waarom?
  //   Vraag: Hoe veel bits moet u instructie address zijn wanneer er maximaal 64 instructies kunnen zijn
  //   Pas de instructie address dan ook aan
endmodule

module ProgramDecoder (
  input  [7:0] Instructie,
  output [1:0] functie_code,
  output [1:0] op_code,
  output [1:0] ri,
  output [1:0] rj,
  output [3:0] Imm
);
endmodule

module regsorFile (
  input  [7:0] Data,
  input  Reset,
  input  Clock,
  input  Write,
  input  [1:0] Ri_Write_read,
  input  [1:0] Rj,
  output [7:0] J,
  output [7:0] I
);

  wire demultiplexer_1_out0, demultiplexer_1_out1, demultiplexer_1_out2, demultiplexer_1_out3;
  wire [7:0] register_1_q, register_2_q, register_3_q, register_4_q;

  Demultiplexer #(.select(2), .enable("false")) demultiplexer_1 (
    .out0(demultiplexer_1_out0), .out1(demultiplexer_1_out1), .out2(demultiplexer_1_out2),
    .out3(demultiplexer_1_out3), .in(Write), .sel(Ri_Write_read));
  Register register_1 (.D(Data), .en(demultiplexer_1_out0), .Q(register_1_q), .clk(Clock), .clr(Reset));
  Register register_2 (.D(Data), .en(demultiplexer_1_out1), .Q(register_2_q), .clk(Clock), .clr(Reset));
  Register register_3 (.D(Data), .en(demultiplexer_1_out2), .Q(register_3_q), .clk(Clock), .clr(Reset));
  Register register_4 (.D(Data), .en(demultiplexer_1_out3), .Q(register_4_q), .clk(Clock), .clr(Reset));
  Multiplexer #(.select(2), .width(8), .enable("false")) multiplexer_1 (
    .in0(register_1_q), .in1(register_2_q), .in2(register_3_q), .in3(register_4_q), .out(I),
    .sel(Ri_Write_read));
  Multiplexer #(.select(2), .width(8), .enable("false")) multiplexer_2 (
    .in0(register_1_q), .in1(register_2_q), .in2(register_3_q), .in3(register_4_q), .out(J), .sel(Rj));
endmodule

module ALU (
  input  Op_code,
  input  [7:0] A,
  input  [7:0] B,
  output [7:0] R
);


  // Notes on the sheet:
  //   Opperaties: AND, OR, ADD, SUB
endmodule
