// Logisim project Examen_template.circ as structural Verilog
module Controller (
  input  [1:0] Function_Code,
  input  [1:0] Op_Code,
  output Branch,
  output Jump,
  output StackRead,
  output StackWrite,
  output RegistorWrite,
  output RegistorRead,
  output [1:0] ALU,
  output Imm_Address,
  output Increase_SP,
  output Decrease_SP
);

  wire demultiplexer_1_out0, demultiplexer_1_out1, demultiplexer_1_out2, demultiplexer_1_out3,
       demultiplexer_2_out0, demultiplexer_2_out1, demultiplexer_2_out2, demultiplexer_2_out3, or_1_out;

  Demultiplexer #(.select(2), .enable("false")) demultiplexer_1 (
    .out0(demultiplexer_1_out0), .out1(demultiplexer_1_out1), .out2(demultiplexer_1_out2),
    .out3(demultiplexer_1_out3), .in(1'b1), .sel(Function_Code));
  Demultiplexer #(.select(2), .enable("false")) demultiplexer_2 (
    .out0(demultiplexer_2_out0), .out1(demultiplexer_2_out1), .out2(demultiplexer_2_out2),
    .out3(demultiplexer_2_out3), .in(1'b1), .sel(Op_Code));
  or or_1 (or_1_out, demultiplexer_2_out0, demultiplexer_2_out1, demultiplexer_2_out2, demultiplexer_2_out3);
  and and_1 (StackWrite, demultiplexer_1_out0, or_1_out);

  // Notes on the sheet:
  //   & meer
endmodule

module Datapad (
  input  C,
  input  R
);


  // Notes on the sheet:
  //   LDI -> LDI r5 2 -> r5 = 2
  //   CLR -> SP = SP - 1
  //   Functionaliteiten: ALU, LDI, POP, PUSH, CLR, JUMP, BRNZ
  //   POP -> POP r1 -> r1 = MEM[SP-1]; SP = SP -1; PC = PC +1
  //   PUSH -> PUSH r1 -> MEM[SP-1] = r1; SP = SP + 1; PC = PC + 1
endmodule

module PC (
  input  [7:0] Offset,
  input  Branch,
  input  Branch_2,
  output [7:0] Instructie_address
);

  wire button_1_out, clock_1_out;
  wire [7:0] adder_1_out, adder_2_out, multiplexer_1_out, multiplexer_2_out;

  Adder adder_1 (.a(Instructie_address), .b(8'h1), .out(adder_1_out));  // open: cin, cout
  Multiplexer #(.width(8), .enable("false")) multiplexer_1 (
    .in0(adder_1_out), .in1(Offset), .out(multiplexer_1_out), .sel(Branch));
  Adder adder_2 (.a(adder_1_out), .b(Offset), .out(adder_2_out));  // open: cin, cout
  Multiplexer #(.width(8), .enable("false")) multiplexer_2 (
    .in0(multiplexer_1_out), .in1(adder_2_out), .out(multiplexer_2_out), .sel(Branch_2));
  Clock clock_1 (.out(clock_1_out));
  Register register_1 (
    .D(multiplexer_2_out), .Q(Instructie_address), .clk(clock_1_out), .clr(button_1_out));  // open: en
  Button button_1 (.out(button_1_out));

  // Notes on the sheet:
  //   Antwoord: 6 -> 2^6 = 64
  //   Vraag: Is de program counter signed of unsigned? Waarom?
  //   Vraag: Hoe veel bits moet u instructie address zijn wanneer er maximaal 64 instructies kunnen zijn
  //   Pas de instructie address dan ook aan
endmodule

module ProgramDecoder (
  input  [8:0] Instructie,
  output [1:0] functie_code,
  output [1:0] op_code,
  output [1:0] ri,
  output [1:0] rj,
  output [3:0] Imm
);
endmodule

module regsorFile (
  input  [7:0] Data,
  input  Reset,
  input  Clock,
  input  Write,
  input  [1:0] Ri_Write_read,
  input  [1:0] Rj,
  output [7:0] J,
  output [7:0] I
);

  wire demultiplexer_1_out0, demultiplexer_1_out1, demultiplexer_1_out2, demultiplexer_1_out3;
  wire [7:0] register_1_q, register_2_q, register_3_q, register_4_q;

  Demultiplexer #(.select(2), .enable("false")) demultiplexer_1 (
    .out0(demultiplexer_1_out0), .out1(demultiplexer_1_out1), .out2(demultiplexer_1_out2),
    .out3(demultiplexer_1_out3), .in(Write), .sel(Ri_Write_read));
  Register register_1 (.D(Data), .en(demultiplexer_1_out0), .Q(register_1_q), .clk(Clock), .clr(Reset));
  Register register_2 (.D(Data), .en(demultiplexer_1_out1), .Q(register_2_q), .clk(Clock), .clr(Reset));
  Register register_3 (.D(Data), .en(demultiplexer_1_out2), .Q(register_3_q), .clk(Clock), .clr(Reset));
  Register register_4 (.D(Data), .en(demultiplexer_1_out3), .Q(register_4_q), .clk(Clock), .clr(Reset));
  Multiplexer #(.select(2), .width(8), .enable("false")) multiplexer_1 (
    .in0(register_1_q), .in1(register_2_q), .in2(register_3_q), .in3(register_4_q), .out(I),
    .sel(Ri_Write_read));
  Multiplexer #(.select(2), .width(8), .enable("false")) multiplexer_2 (
    .in0(register_1_q), .in1(register_2_q), .in2(register_3_q), .in3(register_4_q), .out(J), .sel(Rj));
endmodule

module ALU (
  input  [7:0] A,
  input  [7:0] B,
  input  [1:0] Op_code,
  output [7:0] R
);

  wire [7:0] adder_1_out, not_1_out, or_1_out, subtractor_1_out;

  Adder adder_1 (.a(A), .b(B), .out(adder_1_out));  // open: cin, cout
  Subtractor subtractor_1 (.a(A), .b(B), .out(subtractor_1_out));  // open: bin, bout
  assign not_1_out = ~A;  // NOT_Gate not_1, 8 bits wide
  assign or_1_out = A | A;  // OR_Gate or_1, 8 bits wide
  Multiplexer #(.select(2), .width(8), .enable("false")) multiplexer_1 (
    .in0(or_1_out), .in1(adder_1_out), .in2(subtractor_1_out), .in3(not_1_out), .out(R), .sel(Op_code));

  // Notes on the sheet:
  //   Opperaties: AND, OR, ADD, SUB
endmodule
