// Logisim project opgave5.circ as structural Verilog: 1 circuit, main circuit main
module main (
  input  [2:0] in_1
);

  wire _0_out, _1_out, _2_out, _3_out, _4_out, _5_out, _6_out, _7_out, A_out, B_out, C_out, D_out, E_out,
       F_out, G_out, not_1_out, not_2_out, not_3_out;

  not not_1 (not_1_out, in_1[2]);
  not not_2 (not_2_out, in_1[1]);
  not not_3 (not_3_out, in_1[0]);
  and _0 (_0_out, not_1_out, not_2_out, not_3_out);
  or A (A_out, _2_out, _3_out, _4_out, _5_out, _6_out);
  and _1 (_1_out, not_1_out, not_2_out, in_1[0]);
  or B (B_out, _0_out, _4_out, _5_out, _6_out);
  and _2 (_2_out, not_1_out, in_1[1], not_3_out);
  or C (C_out, _0_out, _2_out, _3_out, _5_out, _6_out, _7_out);
  and _3 (_3_out, not_1_out, in_1[1], in_1[0]);
  or D (D_out, _0_out, _1_out, _2_out, _3_out, _4_out, _7_out);
  _7_Segment_Display u_7_segment_display_1 (
    .g(A_out), .f(B_out), .a(C_out), .b(D_out), .e(E_out), .d(F_out), .c(G_out));  // open: dp
  and _4 (_4_out, in_1[2], not_2_out, not_3_out);
  or E (E_out, _0_out, _2_out, _6_out);
  and _5 (_5_out, in_1[2], not_2_out, in_1[0]);
  or F (F_out, _0_out, _2_out, _3_out, _5_out, _6_out);
  and _6 (_6_out, in_1[2], in_1[1], not_3_out);
  and _7 (_7_out, in_1[2], in_1[1], in_1[0]);
  or G (G_out, _0_out, _1_out, _3_out, _4_out, _5_out, _6_out, _7_out);

  // Notes on the sheet:
  //   <--- 6
  //   <--- 5
  //   <--- 4
  //   <--- 3
  //   <--- 2
  //   <--- 1
  //   <--- 0
  //   <--- 7
  //   Alle inputs die nodig zijn een getal komen uit een lijn.
endmodule
