// Logisim project Opgave1.circ as structural Verilog: 2 circuits, main circuit main
module main (
  input  in_1,
  input  [11:0] in_2,
  input  [11:0] in_3,
  output [11:0] out_4
);

  wire n1_bit_adder_1_carry_out, n1_bit_adder_2_carry_out, n1_bit_adder_3_carry_out,
       n1_bit_adder_4_carry_out, n1_bit_adder_5_carry_out, n1_bit_adder_6_carry_out,
       n1_bit_adder_7_carry_out, n1_bit_adder_8_carry_out, n1_bit_adder_9_carry_out,
       n1_bit_adder_10_carry_out, n1_bit_adder_11_carry_out;

  _1_Bit_Adder u_1_bit_adder_1 (
    .A(in_2[0]), .B(in_3[0]), .Sum(out_4[0]), .Carry_out(n1_bit_adder_1_carry_out), .Carry_in(in_1));
  _1_Bit_Adder u_1_bit_adder_2 (
    .A(in_2[1]), .B(in_3[1]), .Sum(out_4[1]), .Carry_out(n1_bit_adder_2_carry_out),
    .Carry_in(n1_bit_adder_1_carry_out));
  _1_Bit_Adder u_1_bit_adder_3 (
    .A(in_2[2]), .B(in_3[2]), .Sum(out_4[2]), .Carry_out(n1_bit_adder_3_carry_out),
    .Carry_in(n1_bit_adder_2_carry_out));
  _1_Bit_Adder u_1_bit_adder_4 (
    .A(in_2[3]), .B(in_3[3]), .Sum(out_4[3]), .Carry_out(n1_bit_adder_4_carry_out),
    .Carry_in(n1_bit_adder_3_carry_out));
  _1_Bit_Adder u_1_bit_adder_5 (
    .A(in_2[4]), .B(in_3[4]), .Sum(out_4[4]), .Carry_out(n1_bit_adder_5_carry_out),
    .Carry_in(n1_bit_adder_4_carry_out));
  _1_Bit_Adder u_1_bit_adder_6 (
    .A(in_2[5]), .B(in_3[5]), .Sum(out_4[5]), .Carry_out(n1_bit_adder_6_carry_out),
    .Carry_in(n1_bit_adder_5_carry_out));
  _1_Bit_Adder u_1_bit_adder_7 (
    .A(in_2[6]), .B(in_3[6]), .Sum(out_4[6]), .Carry_out(n1_bit_adder_7_carry_out),
    .Carry_in(n1_bit_adder_6_carry_out));
  _1_Bit_Adder u_1_bit_adder_8 (
    .A(in_2[7]), .B(in_3[7]), .Sum(out_4[7]), .Carry_out(n1_bit_adder_8_carry_out),
    .Carry_in(n1_bit_adder_7_carry_out));
  _1_Bit_Adder u_1_bit_adder_9 (
    .A(in_2[8]), .B(in_3[8]), .Sum(out_4[8]), .Carry_out(n1_bit_adder_9_carry_out),
    .Carry_in(n1_bit_adder_8_carry_out));
  _1_Bit_Adder u_1_bit_adder_10 (
    .A(in_2[9]), .B(in_3[9]), .Sum(out_4[9]), .Carry_out(n1_bit_adder_10_carry_out),
    .Carry_in(n1_bit_adder_9_carry_out));
  _1_Bit_Adder u_1_bit_adder_11 (
    .A(in_2[10]), .B(in_3[10]), .Sum(out_4[10]), .Carry_out(n1_bit_adder_11_carry_out),
    .Carry_in(n1_bit_adder_10_carry_out));
  _1_Bit_Adder u_1_bit_adder_12 (
    .A(in_2[11]), .B(in_3[11]), .Sum(out_4[11]), .Carry_in(n1_bit_adder_11_carry_out));  // open: Carry_out
endmodule

// 1-Bit
module _1_Bit_Adder (
  input  Carry_in,
  input  A,
  input  B,
  output Sum,
  output Carry_out
);

  wire and_1_out, and_2_out, xor_1_out;

  xor xor_1 (xor_1_out, A, B);
  and and_1 (and_1_out, A, B);
  and and_2 (and_2_out, Carry_in, xor_1_out);
  xor xor_2 (Sum, Carry_in, xor_1_out);
  or or_1 (Carry_out, and_2_out, and_1_out);
endmodule
