// Logisim project Voorbeeld Examen 22-23 eerste_zit again.circ as structural Verilog: 6 circuits, main circuit main
module main (
  input  reset,
  output [8:0] out_2
);

  wire and_1_out, clock_out, comparator_1_eq, controller_1_brnz, controller_1_jal, controller_1_jump,
       controller_1_load, controller_1_mem_read, controller_1_mem_write, controller_1_unairy,
       controller_1_zero, not_1_out, or_1_out, or_2_out;
  wire [1:0] controller_1_alu_op;
  wire [2:0] decoder_1_func_code, decoder_1_op_code, decoder_1_rs, decoder_1_rt;
  wire [7:0] alu_1_output, decoder_1_off_addr, multiplexer_1_out, multiplexer_2_out, multiplexer_3_out,
       multiplexer_4_out, pc_1_instruction_adress, ram_2_data, registers_1_ap, registers_1_rs_2,
       registers_1_rt_2;

  Clock clock (.out(clock_out));
  PC pc_1 (
    .absolute(or_1_out), .relative(and_1_out), .offset(decoder_1_off_addr), .reset(reset), .clock(clock_out),
    .instruction_adress(pc_1_instruction_adress));
  decoder decoder_1 (
    .in_1(out_2), .OP_CODE(decoder_1_op_code), .Func_Code(decoder_1_func_code), .Rs(decoder_1_rs),
    .Rt(decoder_1_rt), .off_addr(decoder_1_off_addr));
  controller controller_1 (
    .OP_Code(decoder_1_op_code), .Func_Code(decoder_1_func_code), .Unairy(controller_1_unairy),
    .brnz(controller_1_brnz), .jump(controller_1_jump), .jal(controller_1_jal), .ALU_OP(controller_1_alu_op),
    .Mem_Write(controller_1_mem_write), .Mem_Read(controller_1_mem_read), .zero(controller_1_zero),
    .Load(controller_1_load));
  RAM #(.dataWidth(9)) ram_1 (.addr(pc_1_instruction_adress), .data(out_2));  // open: sel, clk, ld, clr
  or or_1 (or_1_out, controller_1_jump, controller_1_jal);
  and and_1 (and_1_out, not_1_out, controller_1_brnz);
  Comparator comparator_1 (.a(ram_2_data), .b({8{1'b0}}), .eq(comparator_1_eq));  // open: gt, lt
  or or_2 (or_2_out, controller_1_unairy, controller_1_load);
  Multiplexer #(.width(8)) multiplexer_1 (
    .in0(multiplexer_2_out), .in1(ram_2_data), .out(multiplexer_1_out), .sel(controller_1_load));  // open: en
  Multiplexer #(.width(8)) multiplexer_2 (
    .in0(alu_1_output), .in1({8{1'b0}}), .out(multiplexer_2_out), .sel(controller_1_zero));  // open: en
  not not_1 (not_1_out, comparator_1_eq);
  registers registers_1 (
    .write_register(or_2_out), .Rs(decoder_1_rs), .Rt(decoder_1_rt), .Rd(decoder_1_rs),
    .DATA(multiplexer_1_out), .reset(reset), .clock(clock_out), .Rs_2(registers_1_rs_2),
    .Rt_2(registers_1_rt_2), .AP(registers_1_ap));
  Multiplexer #(.width(8)) multiplexer_3 (
    .in0(registers_1_rt_2), .in1(8'h1), .out(multiplexer_3_out), .sel(controller_1_unairy));  // open: en
  Multiplexer #(.width(8)) multiplexer_4 (
    .in0(alu_1_output), .in1(pc_1_instruction_adress), .out(multiplexer_4_out), .sel(controller_1_jal));  // open: en
  ALU alu_1 (.A(registers_1_rs_2), .B(multiplexer_3_out), .in_1(controller_1_alu_op), .\output (alu_1_output));
  RAM #(.bus("separate")) ram_2 (
    .addr(registers_1_ap), .din(multiplexer_4_out), .data(ram_2_data), .str(controller_1_mem_write),
    .clk(clock_out), .ld(controller_1_mem_read), .clr(reset));  // open: sel
endmodule

module PC (
  input  absolute,
  input  relative,
  input  [7:0] offset,
  input  reset,
  input  clock,
  output [7:0] instruction_adress
);

  wire not_1_out, or_1_out;
  wire [7:0] adder_1_out, adder_2_out, multiplexer_1_out;

  Adder adder_1 (.a(adder_2_out), .b(offset), .out(adder_1_out));  // open: cin, cout
  or or_1 (or_1_out, relative, absolute);
  Multiplexer #(.width(8)) multiplexer_1 (
    .in0(offset), .in1(adder_1_out), .out(multiplexer_1_out), .sel(relative));  // open: en
  Counter counter_1 (
    .load(or_1_out), .D(multiplexer_1_out), .count(not_1_out), .Q(instruction_adress), .clk(clock),
    .clr(reset));  // open: carry
  not not_1 (not_1_out, or_1_out);
  Adder adder_2 (.a(instruction_adress), .b(8'h1), .out(adder_2_out));  // open: cin, cout
endmodule

module ALU (
  input  [1:0] in_1,
  input  [7:0] A,
  input  [7:0] B,
  output [7:0] \output 
);

  wire [7:0] adder_1_out, not_1_out, or_1_out, subtractor_1_out;

  assign or_1_out = A | B;  // OR_Gate or_1, 8 bits wide
  Adder adder_1 (.a(A), .b(B), .out(adder_1_out));  // open: cin, cout
  Subtractor subtractor_1 (.a(A), .b(B), .out(subtractor_1_out));  // open: bin, bout
  assign not_1_out = ~A;  // NOT_Gate not_1, 8 bits wide
  Multiplexer #(.select(2), .width(8)) multiplexer_1 (
    .in0(or_1_out), .in1(adder_1_out), .in2(subtractor_1_out), .in3(not_1_out), .out(\output ), .sel(in_1));  // open: en
endmodule

module registers (
  input  write_register,
  input  [2:0] Rs,
  input  [2:0] Rt,
  input  [2:0] Rd,
  input  [7:0] DATA,
  input  reset,
  input  clock,
  output [7:0] Rs_2,
  output [7:0] Rt_2,
  output [7:0] AP
);

  wire demultiplexer_1_out0, demultiplexer_1_out1, demultiplexer_1_out2, demultiplexer_1_out3,
       demultiplexer_1_out4, demultiplexer_1_out5, demultiplexer_1_out6, demultiplexer_1_out7;
  wire [7:0] register_1_q, register_2_q, register_3_q, register_4_q, register_5_q, register_6_q, register_7_q;

  Demultiplexer #(.select(3)) demultiplexer_1 (
    .out0(demultiplexer_1_out0), .out1(demultiplexer_1_out1), .out2(demultiplexer_1_out2),
    .out3(demultiplexer_1_out3), .out4(demultiplexer_1_out4), .out5(demultiplexer_1_out5),
    .out6(demultiplexer_1_out6), .out7(demultiplexer_1_out7), .in(write_register), .sel(Rd));  // open: en
  Register register_1 (.en(demultiplexer_1_out0), .Q(register_1_q), .clk(clock), .clr(reset));  // open: D
  Register register_2 (.D(DATA), .en(demultiplexer_1_out1), .Q(register_2_q), .clk(clock), .clr(reset));
  Register register_3 (.D(DATA), .en(demultiplexer_1_out2), .Q(register_3_q), .clk(clock), .clr(reset));
  Register register_4 (.D(DATA), .en(demultiplexer_1_out3), .Q(register_4_q), .clk(clock), .clr(reset));
  Register register_5 (.D(DATA), .en(demultiplexer_1_out4), .Q(register_5_q), .clk(clock), .clr(reset));
  Register register_6 (.D(DATA), .en(demultiplexer_1_out5), .Q(register_6_q), .clk(clock), .clr(reset));
  Register register_7 (.D(DATA), .en(demultiplexer_1_out6), .Q(register_7_q), .clk(clock), .clr(reset));
  Register register_8 (.D(DATA), .en(demultiplexer_1_out7), .Q(AP), .clk(clock), .clr(reset));
  Multiplexer #(.select(3), .width(8)) multiplexer_1 (
    .in0(register_1_q), .in1(register_2_q), .in2(register_3_q), .in3(register_4_q), .in4(register_5_q),
    .in5(register_6_q), .in6(register_7_q), .in7(AP), .out(Rs_2), .sel(Rs));  // open: en
  Multiplexer #(.select(3), .width(8)) multiplexer_2 (
    .in0(register_1_q), .in1(register_2_q), .in2(register_3_q), .in3(register_4_q), .in4(register_5_q),
    .in5(register_6_q), .in6(register_7_q), .in7(AP), .out(Rt_2), .sel(Rt));  // open: en
endmodule

module decoder (
  input  [8:0] in_1,
  output [2:0] OP_CODE,
  output [2:0] Func_Code,
  output [2:0] Rs,
  output [2:0] Rt,
  output [7:0] off_addr
);


  assign Func_Code = in_1[2:0];
  assign off_addr = {{3{in_1[5]}}, in_1[4:0]};
  assign OP_CODE = in_1[8:6];
  assign Rs = in_1[5:3];
  assign Rt = in_1[2:0];
endmodule

module controller (
  input  [2:0] OP_Code,
  input  [2:0] Func_Code,
  output Unairy,
  output brnz,
  output jump,
  output jal,
  output [1:0] ALU_OP,
  output Mem_Write,
  output Mem_Read,
  output zero,
  output Load
);

  wire and_1_out, decoder_1_out0, decoder_1_out4, decoder_1_out5, decoder_2_out0, decoder_2_out4,
       decoder_2_out5, decoder_2_out6, decoder_2_out7, not_1_out;

  Decoder #(.select(3)) decoder_1 (
    .out0(decoder_1_out0), .out4(decoder_1_out4), .out5(decoder_1_out5), .sel(Func_Code));  // open: out1, out2, out3, out6, out7, en
  Decoder #(.select(3)) decoder_2 (
    .out0(decoder_2_out0), .out1(brnz), .out2(jump), .out3(jal), .out4(decoder_2_out4),
    .out5(decoder_2_out5), .out6(decoder_2_out6), .out7(decoder_2_out7), .sel(OP_Code));  // open: en
  and and_1 (and_1_out, decoder_2_out0, decoder_1_out5);
  not not_1 (not_1_out, decoder_1_out5);
  and and_2 (Load, decoder_1_out4, decoder_2_out0);
  and and_3 (Unairy, decoder_2_out0, not_1_out);
  Multiplexer #(.width(2)) multiplexer_1 (
    .in0(OP_Code[1:0]), .in1(Func_Code[1:0]), .out(ALU_OP), .sel(decoder_2_out0));  // open: en
  or or_1 (Mem_Write, and_1_out, jal, decoder_2_out4, decoder_2_out5, decoder_2_out6, decoder_2_out7);
  or or_2 (Mem_Read, Load, brnz);
  and and_4 (zero, decoder_2_out0, decoder_1_out0);
endmodule
