// Logisim project opgave1.circ as structural Verilog: 1 circuit, main circuit main
module main (
  input  a,
  input  b,
  input  in_3,
  input  in_4,
  output out_5,
  output out_6,
  output out_7,
  output out_8
);

  wire and_2_out, not_1_out, not_2_out, not_3_out, not_4_out, or_1_out;

  not not_1 (not_1_out, a);
  not not_2 (not_2_out, b);
  not not_3 (not_3_out, in_3);
  not not_4 (not_4_out, in_4);
  or or_1 (or_1_out, b, a);
  and and_1 (out_6, not_1_out, not_2_out);
  or or_2 (out_7, not_3_out, not_4_out);
  and and_2 (and_2_out, in_4, in_3);
  not not_5 (out_5, or_1_out);
  not not_6 (out_8, and_2_out);
endmodule
