// Logisim project opgave3.circ as structural Verilog: 1 circuit, main circuit main
module main (
  input  in_1,
  input  in_2,
  output out_3,
  output out_4,
  output out_5,
  output out_6,
  output out_7,
  output out_8
);

  wire nand_2_out, nand_4_out, nand_6_out;

  not not_1 (out_3, in_1);
  not nand_1 (out_4, in_1);  // NAND_Gate
  nand nand_2 (nand_2_out, in_1, in_2);
  not nand_3 (out_5, nand_2_out);  // NAND_Gate
  and and_1 (out_6, in_1, in_2);
  not nand_4 (nand_4_out, in_1);  // NAND_Gate
  nand nand_5 (out_7, nand_4_out, nand_6_out);
  not nand_6 (nand_6_out, in_2);  // NAND_Gate
  or or_1 (out_8, in_1, in_2);
endmodule
