// Logisim project Opgave2.circ as structural Verilog: 2 circuits, main circuit main
module main (
  input  [11:0] in_1,
  input  [11:0] in_2,
  input  in_3,
  output [11:0] out_4
);

  wire and_1_out, n1_bit_adder_1_carry_out, n1_bit_adder_2_carry_out, n1_bit_adder_3_carry_out,
       n1_bit_adder_4_carry_out, n1_bit_adder_5_carry_out, n1_bit_adder_6_carry_out,
       n1_bit_adder_7_carry_out, n1_bit_adder_8_carry_out, n1_bit_adder_9_carry_out,
       n1_bit_adder_10_carry_out, n1_bit_adder_11_carry_out, n1_bit_adder_12_carry_out, xnor_1_out, xor_1_out;

  _1_Bit_Adder u_1_bit_adder_1 (
    .Sum(out_4[0]), .Carry_out(n1_bit_adder_1_carry_out), .Carry_in(in_3), .B(in_1[0]), .A(in_2[0]));
  _1_Bit_Adder u_1_bit_adder_2 (
    .Sum(out_4[1]), .Carry_out(n1_bit_adder_2_carry_out), .Carry_in(n1_bit_adder_1_carry_out), .B(in_1[1]),
    .A(in_2[1]));
  _1_Bit_Adder u_1_bit_adder_3 (
    .Sum(out_4[3]), .Carry_out(n1_bit_adder_3_carry_out), .Carry_in(n1_bit_adder_4_carry_out), .B(in_1[3]),
    .A(in_2[3]));
  _1_Bit_Adder u_1_bit_adder_4 (
    .Sum(out_4[2]), .Carry_out(n1_bit_adder_4_carry_out), .Carry_in(n1_bit_adder_2_carry_out), .B(in_1[2]),
    .A(in_2[2]));
  _1_Bit_Adder u_1_bit_adder_5 (
    .Sum(out_4[4]), .Carry_out(n1_bit_adder_5_carry_out), .Carry_in(n1_bit_adder_3_carry_out), .B(in_1[4]),
    .A(in_2[4]));
  _1_Bit_Adder u_1_bit_adder_6 (
    .Sum(out_4[5]), .Carry_out(n1_bit_adder_6_carry_out), .Carry_in(n1_bit_adder_5_carry_out), .B(in_1[5]),
    .A(in_2[5]));
  _1_Bit_Adder u_1_bit_adder_7 (
    .Sum(out_4[6]), .Carry_out(n1_bit_adder_7_carry_out), .Carry_in(n1_bit_adder_6_carry_out), .B(in_1[6]),
    .A(in_2[6]));
  _1_Bit_Adder u_1_bit_adder_8 (
    .Sum(out_4[7]), .Carry_out(n1_bit_adder_8_carry_out), .Carry_in(n1_bit_adder_7_carry_out), .B(in_1[7]),
    .A(in_2[7]));
  _1_Bit_Adder u_1_bit_adder_9 (
    .Sum(out_4[9]), .Carry_out(n1_bit_adder_9_carry_out), .Carry_in(n1_bit_adder_10_carry_out), .B(in_1[9]),
    .A(in_2[9]));
  _1_Bit_Adder u_1_bit_adder_10 (
    .Sum(out_4[8]), .Carry_out(n1_bit_adder_10_carry_out), .Carry_in(n1_bit_adder_8_carry_out), .B(in_1[8]),
    .A(in_2[8]));
  _1_Bit_Adder u_1_bit_adder_11 (
    .Sum(out_4[11]), .Carry_out(n1_bit_adder_11_carry_out), .Carry_in(n1_bit_adder_12_carry_out),
    .B(in_1[11]), .A(in_2[11]));
  _1_Bit_Adder u_1_bit_adder_12 (
    .Sum(out_4[10]), .Carry_out(n1_bit_adder_12_carry_out), .Carry_in(n1_bit_adder_9_carry_out),
    .B(in_1[10]), .A(in_2[10]));
  xnor xnor_1 (xnor_1_out, in_1[11], in_2[11]);
  xor xor_1 (xor_1_out, n1_bit_adder_11_carry_out, out_4[11]);
  and and_1 (and_1_out, xnor_1_out, xor_1_out);
  LED led_1 (.in(and_1_out));
endmodule

// 1-Bit
module _1_Bit_Adder (
  input  Carry_in,
  input  A,
  input  B,
  output Sum,
  output Carry_out
);

  wire and_1_out, and_2_out, xor_1_out;

  xor xor_1 (xor_1_out, A, B);
  and and_1 (and_1_out, A, B);
  and and_2 (and_2_out, Carry_in, xor_1_out);
  xor xor_2 (Sum, Carry_in, xor_1_out);
  or or_1 (Carry_out, and_2_out, and_1_out);
endmodule
