// Logisim project Opgave4.circ as structural Verilog: 5 circuits, main circuit main
module main (
  input  in_1,
  input  [11:0] in_2,
  input  [11:0] in_3,
  output [11:0] out_4,
  output [11:0] out_5
);

  wire carry_lookahead_4bit_1_c1, carry_lookahead_4bit_1_c2, carry_lookahead_4bit_1_c3, n4_bit_adder_1_g0,
       n4_bit_adder_1_p0, n4_bit_adder_2_g0, n4_bit_adder_2_p0, n4_bit_adder_3_g0, n4_bit_adder_3_p0;

  _4_Bit_Adder u_4_bit_adder_1 (
    .Carry_in(in_1), .A(in_2[3:0]), .B(in_3[3:0]), .P0(n4_bit_adder_1_p0), .G0(n4_bit_adder_1_g0),
    .SUM_0_1_2_3(out_4[3:0]));
  _4_Bit_Adder u_4_bit_adder_2 (
    .Carry_in(carry_lookahead_4bit_1_c1), .A(in_2[7:4]), .B(in_3[7:4]), .P0(n4_bit_adder_2_p0),
    .G0(n4_bit_adder_2_g0), .SUM_0_1_2_3(out_4[7:4]));
  _4_Bit_Adder u_4_bit_adder_3 (
    .Carry_in(carry_lookahead_4bit_1_c2), .A(in_2[11:8]), .B(in_3[11:8]), .P0(n4_bit_adder_3_p0),
    .G0(n4_bit_adder_3_g0), .SUM_0_1_2_3(out_4[11:8]));
  LED led_1 (.in(carry_lookahead_4bit_1_c3));
  _12_Bit_Adder u_12_bit_adder_1 (.in_1(in_2), .in_2(in_3), .in_3(in_1), .out_4(out_5));
  Carry_Lookahead_4bit carry_lookahead_4bit_1 (
    .C0(in_1), .G0(n4_bit_adder_1_g0), .P0(n4_bit_adder_1_p0), .C1(carry_lookahead_4bit_1_c1),
    .G1(n4_bit_adder_2_g0), .P1(n4_bit_adder_2_p0), .C2(carry_lookahead_4bit_1_c2), .G2(n4_bit_adder_3_g0),
    .P2(n4_bit_adder_3_p0), .C3(carry_lookahead_4bit_1_c3));
endmodule

// 1-Bit
module _1_Bit_Adder (
  input  Carry_in,
  input  A,
  input  B,
  output Sum,
  output Carry_out
);

  wire and_1_out, and_2_out, xor_1_out;

  xor xor_1 (xor_1_out, A, B);
  and and_1 (and_1_out, A, B);
  and and_2 (and_2_out, Carry_in, xor_1_out);
  xor xor_2 (Sum, Carry_in, xor_1_out);
  or or_1 (Carry_out, and_2_out, and_1_out);
endmodule

module _4_Bit_Adder (
  input  Carry_in,
  input  [3:0] A,
  input  [3:0] B,
  output [3:0] SUM_0_1_2_3,
  output P0,
  output G0
);

  wire and_2_out, and_3_out, and_4_out, g0_out, g1_out, g2_out, g3_out, n1_bit_adder_1_carry_out,
       n1_bit_adder_2_carry_out, n1_bit_adder_3_carry_out, n1_bit_adder_4_carry_out, p0_out, p1_out, p2_out,
       p3_out;

  and u_g0 (g0_out, A[0], B[0]);
  or u_p0 (p0_out, A[0], B[0]);
  and g1 (g1_out, A[1], B[1]);
  and g2 (g2_out, A[2], B[2]);
  or p1 (p1_out, A[1], B[1]);
  and g3 (g3_out, A[3], B[3]);
  or p2 (p2_out, A[2], B[2]);
  or p3 (p3_out, A[3], B[3]);
  _1_Bit_Adder u_1_bit_adder_1 (
    .Sum(SUM_0_1_2_3[0]), .Carry_out(n1_bit_adder_1_carry_out), .Carry_in(Carry_in), .B(A[0]), .A(B[0]));
  and and_1 (P0, p0_out, p1_out, p2_out, p3_out);
  and and_2 (and_2_out, p1_out, p2_out, p3_out, g0_out);
  and and_3 (and_3_out, g1_out, p2_out, p3_out);
  and and_4 (and_4_out, g2_out, p3_out);
  _1_Bit_Adder u_1_bit_adder_2 (
    .Sum(SUM_0_1_2_3[2]), .Carry_out(n1_bit_adder_2_carry_out), .Carry_in(n1_bit_adder_3_carry_out),
    .B(A[2]), .A(B[2]));
  _1_Bit_Adder u_1_bit_adder_3 (
    .Sum(SUM_0_1_2_3[1]), .Carry_out(n1_bit_adder_3_carry_out), .Carry_in(n1_bit_adder_1_carry_out),
    .B(A[1]), .A(B[1]));
  or or_1 (G0, and_2_out, and_3_out, and_4_out, g3_out);
  LED led_1 (.in(n1_bit_adder_4_carry_out));
  _1_Bit_Adder u_1_bit_adder_4 (
    .Sum(SUM_0_1_2_3[3]), .Carry_out(n1_bit_adder_4_carry_out), .Carry_in(n1_bit_adder_2_carry_out),
    .B(A[3]), .A(B[3]));
endmodule

module Carry_Lookahead_4bit (
  input  C0,
  input  G0,
  input  P0,
  input  G1,
  input  P1,
  input  G2,
  input  P2,
  output C1,
  output C2,
  output C3
);

  wire and_1_out, and_2_out, and_3_out, and_4_out, and_5_out, and_6_out;

  and and_1 (and_1_out, P0, C0);
  or or_1 (C1, G0, and_1_out);
  and and_2 (and_2_out, C0, P0, P1);
  and and_3 (and_3_out, P1, G0);
  or or_2 (C2, and_2_out, and_3_out, G1);
  and and_4 (and_4_out, P2, G1);
  and and_5 (and_5_out, P2, P1, G0);
  or or_3 (C3, G2, and_4_out, and_5_out, and_6_out);
  and and_6 (and_6_out, P2, P1, P0, C0);
endmodule

// Ripple Carry
module _12_Bit_Adder (
  input  [11:0] in_1,
  input  [11:0] in_2,
  input  in_3,
  output [11:0] out_4
);

  wire n1_bit_adder_1_carry_out, n1_bit_adder_2_carry_out, n1_bit_adder_3_carry_out,
       n1_bit_adder_4_carry_out, n1_bit_adder_5_carry_out, n1_bit_adder_6_carry_out,
       n1_bit_adder_7_carry_out, n1_bit_adder_8_carry_out, n1_bit_adder_9_carry_out,
       n1_bit_adder_10_carry_out, n1_bit_adder_11_carry_out, n1_bit_adder_12_carry_out;

  _1_Bit_Adder u_1_bit_adder_1 (
    .Sum(out_4[0]), .Carry_out(n1_bit_adder_1_carry_out), .Carry_in(in_3), .B(in_1[0]), .A(in_2[0]));
  _1_Bit_Adder u_1_bit_adder_2 (
    .Sum(out_4[1]), .Carry_out(n1_bit_adder_2_carry_out), .Carry_in(n1_bit_adder_1_carry_out), .B(in_1[1]),
    .A(in_2[1]));
  _1_Bit_Adder u_1_bit_adder_3 (
    .Sum(out_4[3]), .Carry_out(n1_bit_adder_3_carry_out), .Carry_in(n1_bit_adder_4_carry_out), .B(in_1[3]),
    .A(in_2[3]));
  _1_Bit_Adder u_1_bit_adder_4 (
    .Sum(out_4[2]), .Carry_out(n1_bit_adder_4_carry_out), .Carry_in(n1_bit_adder_2_carry_out), .B(in_1[2]),
    .A(in_2[2]));
  _1_Bit_Adder u_1_bit_adder_5 (
    .Sum(out_4[5]), .Carry_out(n1_bit_adder_5_carry_out), .Carry_in(n1_bit_adder_6_carry_out), .B(in_1[5]),
    .A(in_2[5]));
  _1_Bit_Adder u_1_bit_adder_6 (
    .Sum(out_4[4]), .Carry_out(n1_bit_adder_6_carry_out), .Carry_in(n1_bit_adder_3_carry_out), .B(in_1[4]),
    .A(in_2[4]));
  _1_Bit_Adder u_1_bit_adder_7 (
    .Sum(out_4[6]), .Carry_out(n1_bit_adder_7_carry_out), .Carry_in(n1_bit_adder_5_carry_out), .B(in_1[6]),
    .A(in_2[6]));
  _1_Bit_Adder u_1_bit_adder_8 (
    .Sum(out_4[7]), .Carry_out(n1_bit_adder_8_carry_out), .Carry_in(n1_bit_adder_7_carry_out), .B(in_1[7]),
    .A(in_2[7]));
  _1_Bit_Adder u_1_bit_adder_9 (
    .Sum(out_4[8]), .Carry_out(n1_bit_adder_9_carry_out), .Carry_in(n1_bit_adder_8_carry_out), .B(in_1[8]),
    .A(in_2[8]));
  _1_Bit_Adder u_1_bit_adder_10 (
    .Sum(out_4[9]), .Carry_out(n1_bit_adder_10_carry_out), .Carry_in(n1_bit_adder_9_carry_out), .B(in_1[9]),
    .A(in_2[9]));
  _1_Bit_Adder u_1_bit_adder_11 (
    .Sum(out_4[11]), .Carry_out(n1_bit_adder_11_carry_out), .Carry_in(n1_bit_adder_12_carry_out),
    .B(in_1[11]), .A(in_2[11]));
  _1_Bit_Adder u_1_bit_adder_12 (
    .Sum(out_4[10]), .Carry_out(n1_bit_adder_12_carry_out), .Carry_in(n1_bit_adder_10_carry_out),
    .B(in_1[10]), .A(in_2[10]));
  LED led_1 (.in(n1_bit_adder_11_carry_out));
endmodule
