// Logisim project Opgave4 opdracht 3 AF niet in juist doc.circ as structural Verilog: 18 circuits, main circuit main
module main (
  input  [3:0] in_1,
  input  [11:0] in_2,
  input  [11:0] in_3,
  output [11:0] out_4,
  output overflow
);

  wire of_add, of_inv, of_sla, of_sub;
  wire [11:0] add, \and , eq, gt, inv, lt, neq, \not , \or , sla, sll, sra, srl, sub, zero;

  add add_1 (.in_1(in_2), .in_2(in_3), .out_3(add), .OF(of_add));
  sub sub_1 (.in_1(in_2), .in_2(in_3), .out_3(sub), .OF(of_sub));
  \and  and_1 (.in_1(in_2), .in_2(in_3), .out_3(\and ));
  \or  or_1 (.in_1(in_2), .in_2(in_3), .out_3(\or ));
  lt__gt__eq__neq lt_gt_eq_neq_1 (.A(in_2), .B(in_3), .A__B(neq), .A_B(eq), .A_B_2(gt), .A_B_3(lt));
  \not  not_1 (.in_1(in_2), .out_2(\not ));
  inv inv_1 (.in_1(in_2), .out_2(inv), .of(of_inv));
  sll sll_1 (.A(in_2), .Shift_left(sll));
  sla sla_1 (.Shift_left(sla), .A(in_2), .of(of_sla));
  srl srl_1 (.A(in_2), .Shift_right_l(srl));
  sra sra_1 (.in_1(in_2), .out_2(sra));
  zero zero_1 (.out_1(zero));
  Multiplexer #(.select(4), .width(12), .enable("false")) multiplexer_1 (
    .in0(add), .in1(sub), .in2(\and ), .in3(\or ), .in4(lt), .in5(gt), .in6(eq), .in7(neq), .in8(\not ),
    .in9(inv), .in10(sll), .in11(srl), .in12(sla), .in13(sra), .in14(zero), .in15(in_2), .out(out_4),
    .sel(in_1));
  Multiplexer #(.select(4), .enable("false")) multiplexer_2 (
    .in0(of_add), .in1(of_sub), .in2(1'b0), .in3(1'b0), .in4(1'b0), .in5(1'b0), .in6(1'b0), .in7(1'b0),
    .in8(1'b0), .in9(of_inv), .in10(1'b0), .in11(1'b0), .in12(of_sla), .in13(1'b0), .in14(1'b0), .in15(1'b0),
    .out(overflow), .sel(in_1));

  // Other names for the same wires on the sheet: B1[11:0] = in_3; A1[11:0] = in_2; noop[11:0] = in_2
endmodule

// 1-Bit
module _1_Bit_Adder (
  input  Carry_in,
  input  A,
  input  B,
  output Sum,
  output Carry_out
);

  wire and_1_out, and_2_out, xor_1_out;

  xor xor_1 (xor_1_out, A, B);
  and and_1 (and_1_out, A, B);
  and and_2 (and_2_out, Carry_in, xor_1_out);
  xor xor_2 (Sum, Carry_in, xor_1_out);
  or or_1 (Carry_out, and_2_out, and_1_out);
endmodule

module _4_Bit_Adder (
  input  Carry_in,
  input  [3:0] A,
  input  [3:0] B,
  output P0,
  output G0,
  output [3:0] SUM_0_1_2_3
);

  wire and_2_out, and_3_out, and_4_out, carry_lookahead_4_inputs_1_c1, carry_lookahead_4_inputs_1_c2,
       carry_lookahead_4_inputs_1_c3, carry_lookahead_4_inputs_1_c4, g0_out, g1_out, g2_out, g3_out,
       n1_bit_adder_4_carry_out, p0_out, p1_out, p2_out, p3_out;

  or or_1 (G0, and_2_out, and_3_out, and_4_out, g3_out);
  and and_1 (P0, p0_out, p1_out, p2_out, p3_out);
  and and_2 (and_2_out, p1_out, p2_out, p3_out, g0_out);
  and and_3 (and_3_out, g1_out, p2_out, p3_out);
  and and_4 (and_4_out, g2_out, p3_out);
  or u_p0 (p0_out, A[0], B[0]);
  and u_g0 (g0_out, A[0], B[0]);
  or p1 (p1_out, A[1], B[1]);
  and g1 (g1_out, A[1], B[1]);
  and g2 (g2_out, A[2], B[2]);
  or p2 (p2_out, A[2], B[2]);
  and g3 (g3_out, A[3], B[3]);
  or p3 (p3_out, A[3], B[3]);
  Carry_Lookahead_4_inputs carry_lookahead_4_inputs_1 (
    .C0(Carry_in), .G0(g0_out), .P0(p0_out), .C1(carry_lookahead_4_inputs_1_c1), .G1(g1_out), .P1(p1_out),
    .C2(carry_lookahead_4_inputs_1_c2), .G2(g2_out), .P2(p2_out), .C3(carry_lookahead_4_inputs_1_c3),
    .G3(g3_out), .P3(p3_out), .C4(carry_lookahead_4_inputs_1_c4));
  LED led_1 (.in(carry_lookahead_4_inputs_1_c4));
  _1_Bit_Adder u_1_bit_adder_1 (.Sum(SUM_0_1_2_3[0]), .Carry_in(Carry_in), .B(A[0]), .A(B[0]));  // open: Carry_out
  _1_Bit_Adder u_1_bit_adder_2 (
    .Sum(SUM_0_1_2_3[1]), .Carry_in(carry_lookahead_4_inputs_1_c1), .B(A[1]), .A(B[1]));  // open: Carry_out
  _1_Bit_Adder u_1_bit_adder_3 (
    .Sum(SUM_0_1_2_3[2]), .Carry_in(carry_lookahead_4_inputs_1_c2), .B(A[2]), .A(B[2]));  // open: Carry_out
  LED led_2 (.in(n1_bit_adder_4_carry_out));
  _1_Bit_Adder u_1_bit_adder_4 (
    .Sum(SUM_0_1_2_3[3]), .Carry_out(n1_bit_adder_4_carry_out), .Carry_in(carry_lookahead_4_inputs_1_c3),
    .B(A[3]), .A(B[3]));
endmodule

// Carry Lookahead
module Carry_Lookahead_3inputs (
  input  C0,
  input  G0,
  input  P0,
  input  G1,
  input  P1,
  input  G2,
  input  P2,
  output C1,
  output C2,
  output C3
);

  wire and_1_out, and_2_out, and_3_out, and_4_out, and_5_out, and_6_out;

  and and_1 (and_1_out, P0, C0);
  or or_1 (C1, G0, and_1_out);
  and and_2 (and_2_out, C0, P0, P1);
  and and_3 (and_3_out, P1, G0);
  or or_2 (C2, and_2_out, and_3_out, G1);
  and and_4 (and_4_out, P2, P1, G0);
  and and_5 (and_5_out, P2, G1);
  or or_3 (C3, G2, and_5_out, and_4_out, and_6_out);
  and and_6 (and_6_out, P2, P1, P0, C0);
endmodule

module add (
  input  [11:0] in_1,
  input  [11:0] in_2,
  output [11:0] out_3,
  output OF
);

  wire carry_lookahead_3inputs_1_c1, carry_lookahead_3inputs_1_c2, carry_lookahead_3inputs_1_c3,
       n4_bit_adder_1_g0, n4_bit_adder_1_p0, n4_bit_adder_2_g0, n4_bit_adder_2_p0, n4_bit_adder_3_g0,
       n4_bit_adder_3_p0, xnor_1_out, xor_1_out;

  xnor xnor_1 (xnor_1_out, in_1[11], in_2[11]);
  _4_Bit_Adder u_4_bit_adder_1 (
    .Carry_in(1'b0), .A(in_1[3:0]), .B(in_2[3:0]), .P0(n4_bit_adder_1_p0), .G0(n4_bit_adder_1_g0),
    .SUM_0_1_2_3(out_3[3:0]));
  _4_Bit_Adder u_4_bit_adder_2 (
    .Carry_in(carry_lookahead_3inputs_1_c1), .A(in_1[7:4]), .B(in_2[7:4]), .P0(n4_bit_adder_2_p0),
    .G0(n4_bit_adder_2_g0), .SUM_0_1_2_3(out_3[7:4]));
  _4_Bit_Adder u_4_bit_adder_3 (
    .Carry_in(carry_lookahead_3inputs_1_c2), .A(in_1[11:8]), .B(in_2[11:8]), .P0(n4_bit_adder_3_p0),
    .G0(n4_bit_adder_3_g0), .SUM_0_1_2_3(out_3[11:8]));
  xor xor_1 (xor_1_out, carry_lookahead_3inputs_1_c3, out_3[11]);
  Carry_Lookahead_3inputs carry_lookahead_3inputs_1 (
    .C0(1'b0), .G0(n4_bit_adder_1_g0), .P0(n4_bit_adder_1_p0), .C1(carry_lookahead_3inputs_1_c1),
    .G1(n4_bit_adder_2_g0), .P1(n4_bit_adder_2_p0), .C2(carry_lookahead_3inputs_1_c2),
    .G2(n4_bit_adder_3_g0), .P2(n4_bit_adder_3_p0), .C3(carry_lookahead_3inputs_1_c3));
  and and_1 (OF, xor_1_out, xnor_1_out);
endmodule

module sub (
  input  [11:0] in_1,
  input  [11:0] in_2,
  output [11:0] out_3,
  output OF
);

  wire carry_lookahead_3inputs_1_c1, carry_lookahead_3inputs_1_c2, carry_lookahead_3inputs_1_c3,
       n4_bit_adder_1_g0, n4_bit_adder_1_p0, n4_bit_adder_2_g0, n4_bit_adder_2_p0, n4_bit_adder_3_g0,
       n4_bit_adder_3_p0, xnor_1_out, xor_1_out;
  wire [11:0] not_1_out;

  xnor xnor_1 (xnor_1_out, in_1[11], not_1_out[11]);
  assign not_1_out = ~in_2;  // NOT_Gate not_1, 12 bits wide
  xor xor_1 (xor_1_out, carry_lookahead_3inputs_1_c3, out_3[11]);
  _4_Bit_Adder u_4_bit_adder_1 (
    .Carry_in(1'b1), .A(in_1[3:0]), .B(not_1_out[3:0]), .P0(n4_bit_adder_1_p0), .G0(n4_bit_adder_1_g0),
    .SUM_0_1_2_3(out_3[3:0]));
  _4_Bit_Adder u_4_bit_adder_2 (
    .Carry_in(carry_lookahead_3inputs_1_c1), .A(in_1[7:4]), .B(not_1_out[7:4]), .P0(n4_bit_adder_2_p0),
    .G0(n4_bit_adder_2_g0), .SUM_0_1_2_3(out_3[7:4]));
  _4_Bit_Adder u_4_bit_adder_3 (
    .Carry_in(carry_lookahead_3inputs_1_c2), .A(in_1[11:8]), .B(not_1_out[11:8]), .P0(n4_bit_adder_3_p0),
    .G0(n4_bit_adder_3_g0), .SUM_0_1_2_3(out_3[11:8]));
  and and_1 (OF, xor_1_out, xnor_1_out);
  Carry_Lookahead_3inputs carry_lookahead_3inputs_1 (
    .C0(1'b1), .G0(n4_bit_adder_1_g0), .P0(n4_bit_adder_1_p0), .C1(carry_lookahead_3inputs_1_c1),
    .G1(n4_bit_adder_2_g0), .P1(n4_bit_adder_2_p0), .C2(carry_lookahead_3inputs_1_c2),
    .G2(n4_bit_adder_3_g0), .P2(n4_bit_adder_3_p0), .C3(carry_lookahead_3inputs_1_c3));
endmodule

module \and  (
  input  [11:0] in_1,
  input  [11:0] in_2,
  output [11:0] out_3
);

  assign out_3 = in_1 & in_2;  // AND_Gate and_1, 12 bits wide
endmodule

module \or  (
  input  [11:0] in_1,
  input  [11:0] in_2,
  output [11:0] out_3
);

  assign out_3 = in_1 | in_2;  // OR_Gate or_1, 12 bits wide
endmodule

module lt__gt__eq__neq (
  input  [11:0] A,
  input  [11:0] B,
  output [11:0] A_B,
  output [11:0] A__B,
  output [11:0] A_B_2,
  output [11:0] A_B_3
);

  wire A_B1, A_B2, A_B3, and_1_out, and_2_out, multiplexer_1_out, multiplexer_2_out, not_1_out, not_2_out,
       sub_1_of, xor_1_out, xor_2_out, xor_3_out;
  wire [11:0] sub_1_out_3;

  _4bit u_4bit_1 (.B(A[3:0]), .A(B[3:0]), .A_B(A_B1));
  _4bit u_4bit_2 (.B(A[7:4]), .A(B[7:4]), .A_B(A_B2));
  _4bit u_4bit_3 (.B(A[11:8]), .A(B[11:8]), .A_B(A_B3));
  sub sub_1 (.in_1(A), .in_2(B), .out_3(sub_1_out_3), .OF(sub_1_of));
  not not_1 (not_1_out, sub_1_out_3[11]);
  xor xor_1 (xor_1_out, sub_1_of, not_1_out);
  xor xor_2 (xor_2_out, sub_1_of, sub_1_out_3[11]);
  Multiplexer #(.enable("false")) multiplexer_1 (.in0(1'b1), .in1(1'b0), .out(multiplexer_1_out), .sel(xor_1_out));
  and and_1 (and_1_out, A_B1, A_B2, A_B3);
  Multiplexer #(.enable("false")) multiplexer_2 (.in0(1'b1), .in1(1'b0), .out(multiplexer_2_out), .sel(xor_2_out));
  assign A_B = {{11{1'b0}}, and_1_out};  // Bit_Extender bit_extender_1
  xor xor_3 (xor_3_out, and_1_out, multiplexer_2_out);
  assign A_B_2 = {{11{1'b0}}, xor_3_out};  // Bit_Extender bit_extender_2
  assign A_B_3 = {{11{1'b0}}, multiplexer_1_out};  // Bit_Extender bit_extender_3
  not not_2 (not_2_out, and_2_out);
  and and_2 (and_2_out, A_B1, A_B2, A_B3);
  assign A__B = {{11{1'b0}}, not_2_out};  // Bit_Extender bit_extender_4
endmodule

// 4bit><=
module _4bit (
  input  [3:0] B,
  input  [3:0] A,
  output A_B
);

  wire and_1_out, and_2_out, and_3_out, and_4_out, and_5_out, and_6_out, and_7_out, and_8_out, not_1_out,
       not_2_out, not_3_out, not_4_out, not_5_out, not_6_out, not_7_out, not_8_out, X0_out, X1_out, X2_out,
       X3_out;

  not not_1 (not_1_out, B[0]);
  not not_2 (not_2_out, A[0]);
  not not_3 (not_3_out, B[1]);
  not not_4 (not_4_out, A[1]);
  not not_5 (not_5_out, B[2]);
  not not_6 (not_6_out, A[2]);
  not not_7 (not_7_out, B[3]);
  not not_8 (not_8_out, A[3]);
  and and_1 (and_1_out, not_1_out, A[0]);
  and and_2 (and_2_out, B[0], not_2_out);
  and and_3 (and_3_out, not_3_out, A[1]);
  and and_4 (and_4_out, B[1], not_4_out);
  and and_5 (and_5_out, not_5_out, A[2]);
  and and_6 (and_6_out, B[2], not_6_out);
  and and_7 (and_7_out, not_7_out, A[3]);
  and and_8 (and_8_out, B[3], not_8_out);
  nor X0 (X0_out, and_1_out, and_2_out);
  nor X1 (X1_out, and_3_out, and_4_out);
  nor X2 (X2_out, and_5_out, and_6_out);
  nor X3 (X3_out, and_7_out, and_8_out);
  and and_9 (A_B, X0_out, X1_out, X2_out, X3_out);
endmodule

module \not  (
  input  [11:0] in_1,
  output [11:0] out_2
);

  assign out_2 = ~in_1;  // NOT_Gate not_1, 12 bits wide
endmodule

module zero (
  output [11:0] out_1
);


  assign out_1 = {12{1'b0}};
endmodule

module sll (
  input  [11:0] A,
  output [11:0] Shift_left
);


  assign Shift_left = {A[10:0], 1'b0};
endmodule

module srl (
  input  [11:0] A,
  output [11:0] Shift_right_l
);


  assign Shift_right_l = {1'b0, A[11:1]};
endmodule

module inv (
  input  [11:0] in_1,
  output [11:0] out_2,
  output of
);

  wire [11:0] bit_extender_1_out, not_1_out;

  assign bit_extender_1_out = {{11{1'b0}}, 1'b1};  // Bit_Extender bit_extender_1
  assign not_1_out = ~in_1;  // NOT_Gate not_1, 12 bits wide
  add add_1 (.in_1(not_1_out), .in_2(bit_extender_1_out), .out_3(out_2), .OF(of));
endmodule

module sla (
  input  [11:0] A,
  output [11:0] Shift_left,
  output of
);

  xor xor_1 (of, A[10], A[11]);

  assign Shift_left = {A[10:0], 1'b0};
endmodule

module Carry_Lookahead_4_inputs (
  input  C0,
  input  G0,
  input  P0,
  input  G1,
  input  P1,
  input  G2,
  input  P2,
  input  G3,
  input  P3,
  output C1,
  output C2,
  output C3,
  output C4
);

  wire and_1_out, and_2_out, and_3_out, and_4_out, and_5_out, and_6_out, and_7_out, and_8_out, and_9_out,
       and_10_out;

  and and_1 (and_1_out, P0, C0);
  or or_1 (C1, G0, and_1_out);
  and and_2 (and_2_out, C0, P0, P1);
  and and_3 (and_3_out, P1, G0);
  or or_2 (C2, and_2_out, and_3_out, G1);
  and and_4 (and_4_out, P2, G1);
  and and_5 (and_5_out, P2, P1, G0);
  or or_3 (C3, G2, and_4_out, and_5_out, and_6_out);
  and and_6 (and_6_out, P2, P1, P0, C0);
  and and_7 (and_7_out, P0, P1, P2, P3, C0);
  and and_8 (and_8_out, P1, P2, P3, G0);
  and and_9 (and_9_out, P2, P3, G1);
  and and_10 (and_10_out, P3, G2);
  or or_4 (C4, and_7_out, and_8_out, and_9_out, and_10_out, G3);
endmodule

module sra (
  input  [11:0] in_1,
  output [11:0] out_2
);


  assign out_2 = {{2{in_1[11]}}, in_1[10:1]};
endmodule
