// Logisim project Opdracht4.5.circ as structural Verilog: 8 circuits, main circuit main
module main (
  input  C,
  input  write,
  input  reset,
  input  [11:0] D,
  output [11:0] out_5
);

  wire and_1_out;

  D_Flip_Flop d_ff_1 (.clk(and_1_out), .D(D[0]), .Q(out_5[0]), .reset(reset));  // open: Qn, preset, en
  D_Flip_Flop d_ff_2 (.clk(and_1_out), .D(D[2]), .Q(out_5[2]), .reset(reset));  // open: Qn, preset, en
  D_Flip_Flop d_ff_3 (.clk(and_1_out), .D(D[1]), .Q(out_5[1]), .reset(reset));  // open: Qn, preset, en
  D_Flip_Flop d_ff_4 (.clk(and_1_out), .D(D[3]), .Q(out_5[3]), .reset(reset));  // open: Qn, preset, en
  D_Flip_Flop d_ff_5 (.clk(and_1_out), .D(D[4]), .Q(out_5[4]), .reset(reset));  // open: Qn, preset, en
  and and_1 (and_1_out, C, write);
  D_Flip_Flop d_ff_6 (.clk(and_1_out), .D(D[5]), .Q(out_5[5]), .reset(reset));  // open: Qn, preset, en
  D_Flip_Flop d_ff_7 (.clk(and_1_out), .D(D[6]), .Q(out_5[6]), .reset(reset));  // open: Qn, preset, en
  D_Flip_Flop d_ff_8 (.clk(and_1_out), .D(D[7]), .Q(out_5[7]), .reset(reset));  // open: Qn, preset, en
  D_Flip_Flop d_ff_9 (.clk(and_1_out), .D(D[8]), .Q(out_5[8]), .reset(reset));  // open: Qn, preset, en
  D_Flip_Flop d_ff_10 (.clk(and_1_out), .D(D[9]), .Q(out_5[9]), .reset(reset));  // open: Qn, preset, en
  D_Flip_Flop d_ff_11 (.clk(and_1_out), .D(D[10]), .Q(out_5[10]), .reset(reset));  // open: Qn, preset, en
  D_Flip_Flop d_ff_12 (.clk(and_1_out), .D(D[11]), .Q(out_5[11]), .reset(reset));  // open: Qn, preset, en
endmodule

module register_file (
  input  [11:0] data,
  input  [2:0] rd,
  input  write,
  input  reset,
  input  C,
  input  [2:0] rs,
  input  [2:0] rt,
  output [11:0] S,
  output [11:0] T
);

  wire [11:0] demultiplexer_1_out0, demultiplexer_1_out1, demultiplexer_1_out2, demultiplexer_1_out3,
       demultiplexer_1_out4, demultiplexer_1_out5, demultiplexer_1_out6, demultiplexer_1_out7, main_1_out_5,
       main_2_out_5, main_3_out_5, main_4_out_5, main_5_out_5, main_6_out_5, main_7_out_5,
       rising_edge_1_out_5;

  Demultiplexer #(.select(3), .width(12), .enable("false")) demultiplexer_1 (
    .out0(demultiplexer_1_out0), .out1(demultiplexer_1_out1), .out2(demultiplexer_1_out2),
    .out3(demultiplexer_1_out3), .out4(demultiplexer_1_out4), .out5(demultiplexer_1_out5),
    .out6(demultiplexer_1_out6), .out7(demultiplexer_1_out7), .in(data), .sel(rd));
  main main_1 (.reset(reset), .D(demultiplexer_1_out0), .write(write), .out_5(main_1_out_5), .C(C));
  rising_edge rising_edge_1 (
    .C(C), .reset(reset), .D(demultiplexer_1_out1), .write(write), .out_5(rising_edge_1_out_5));
  main main_2 (.reset(reset), .D(demultiplexer_1_out2), .write(write), .out_5(main_2_out_5), .C(C));
  main main_3 (.reset(reset), .D(demultiplexer_1_out3), .write(write), .out_5(main_3_out_5), .C(C));
  main main_4 (.reset(reset), .D(demultiplexer_1_out4), .write(write), .out_5(main_4_out_5), .C(C));
  main main_5 (.reset(reset), .D(demultiplexer_1_out5), .write(write), .out_5(main_5_out_5), .C(C));
  main main_6 (.reset(reset), .D(demultiplexer_1_out6), .write(write), .out_5(main_6_out_5), .C(C));
  main main_7 (.reset(reset), .D(demultiplexer_1_out7), .write(write), .out_5(main_7_out_5), .C(C));
  Multiplexer #(.select(3), .width(12), .enable("false")) multiplexer_1 (
    .in0(main_1_out_5), .in1(rising_edge_1_out_5), .in2(main_2_out_5), .in3(main_3_out_5),
    .in4(main_4_out_5), .in5(main_5_out_5), .in6(main_6_out_5), .in7(main_7_out_5), .out(S), .sel(rs));
  Multiplexer #(.select(3), .width(12), .enable("false")) multiplexer_2 (
    .in0(main_1_out_5), .in1(rising_edge_1_out_5), .in2(main_2_out_5), .in3(main_3_out_5),
    .in4(main_4_out_5), .in5(main_5_out_5), .in6(main_6_out_5), .in7(main_7_out_5), .out(T), .sel(rt));
endmodule

// counter add/sub
module counter (
  input  [1:0] in_1,
  input  [11:0] data,
  input  C,
  output [11:0] S
);

  wire comparator_1_eq, comparator_1_lt, comparator_2_eq, comparator_2_gt, multiplexer_2_out, or_1_out,
       or_2_out;
  wire [11:0] add_1_out_3, bit_extender_1_out, multiplexer_1_out, sub_1_out_3;

  assign bit_extender_1_out = {{11{1'b0}}, 1'b1};  // Bit_Extender bit_extender_1
  Comparator #(.width(12), .mode("unsigned")) comparator_1 (
    .a(data), .b(S), .eq(comparator_1_eq), .lt(comparator_1_lt));  // open: gt
  Comparator #(.width(12), .mode("unsigned")) comparator_2 (
    .a({12{1'b0}}), .b(S), .gt(comparator_2_gt), .eq(comparator_2_eq));  // open: lt
  add add_1 (.in_1(S), .in_2(bit_extender_1_out), .out_3(add_1_out_3));  // open: OF
  sub sub_1 (.in_1(S), .in_2(bit_extender_1_out), .out_3(sub_1_out_3));  // open: OF
  or or_1 (or_1_out, comparator_1_eq, comparator_1_lt);
  or or_2 (or_2_out, comparator_2_gt, comparator_2_eq);
  Multiplexer #(.select(2), .width(12), .enable("false")) multiplexer_1 (
    .in0(data), .in1(add_1_out_3), .in2(sub_1_out_3), .out(multiplexer_1_out), .sel(in_1));  // open: in3
  Multiplexer #(.select(2), .enable("false")) multiplexer_2 (
    .in0(1'b0), .in1(or_1_out), .in2(or_2_out), .in3(1'b0), .out(multiplexer_2_out), .sel(in_1));
  register_file register_file_1 (
    .S(S), .data(multiplexer_1_out), .rd(3'b000), .write(1'b1), .reset(multiplexer_2_out), .C(C), .rs(3'b000));  // open: T, rt
endmodule

module stack (
  input  reset,
  input  pop,
  input  push,
  input  [11:0] data,
  output ERROR,
  output [11:0] Top_of_stack
);

  wire and_1_out, and_2_out, and_3_out, and_4_out, clock, clock_1_out, comparator_1_eq, comparator_2_eq,
       controlled_buffer_3_out, controlled_buffer_4_out, not_1_out, not_2_out, not_3_out, not_4_out,
       or_1_out, or_2_out, pop_or_push, pop_or_push_or_reset, xor_1_out;
  wire [1:0] controlled_buffer_1_out;
  wire [11:0] data_t, pointer, top;

  Clock clock_1 (.out(clock_1_out));
  or or_1 (or_1_out, pop, reset);
  assign controlled_buffer_1_out = push ? 2'b01 : 2'bz;  // Controlled_Buffer controlled_buffer_1
  assign controlled_buffer_1_out = or_1_out ? 2'b10 : 2'bz;  // Controlled_Buffer controlled_buffer_2
  assign controlled_buffer_3_out = xor_1_out ? clock_1_out : 1'bz;  // Controlled_Buffer controlled_buffer_3
  counter_zonder_stop counter_zonder_stop_1 (
    .in_1(controlled_buffer_1_out), .Reset(reset), .C(controlled_buffer_3_out), .S(pointer));
  // Probe on pointer
  Comparator #(.width(12)) comparator_1 (.a({12{1'b0}}), .b(top), .eq(comparator_1_eq));  // open: gt, lt
  Comparator #(.width(12)) comparator_2 (.a({12{1'b0}}), .b(pointer), .eq(comparator_2_eq));  // open: gt, lt
  not not_1 (not_1_out, comparator_1_eq);
  and and_1 (and_1_out, not_1_out, comparator_2_eq, pop);
  and and_2 (and_2_out, comparator_2_eq, push, comparator_1_eq);
  not not_2 (not_2_out, and_2_out);
  xor xor_1 (xor_1_out, and_1_out, not_2_out);
  or or_2 (or_2_out, pop, reset);
  assign controlled_buffer_4_out = push ? 1'b1 : 1'bz;  // Controlled_Buffer controlled_buffer_4
  assign controlled_buffer_4_out = or_2_out ? 1'b0 : 1'bz;  // Controlled_Buffer controlled_buffer_5
  Multiplexer #(.enable("false")) multiplexer_1 (
    .in0(clock_1_out), .in1(not_3_out), .out(clock), .sel(controlled_buffer_4_out));
  not not_3 (not_3_out, clock_1_out);
  not not_4 (not_4_out, pop);
  assign data_t = not_4_out ? data : 12'bz;  // Controlled_Buffer controlled_buffer_6
  assign data_t = pop ? {12{1'b0}} : 12'bz;  // Controlled_Buffer controlled_buffer_7
  RAM #(.addrWidth(12), .dataWidth(12), .bus("separate")) ram_1 (
    .addr(pointer), .din(data_t), .data(top), .str(pop_or_push_or_reset), .clk(clock), .clr(reset));  // open: sel, ld
  // Probe on top
  and and_3 (and_3_out, pop, comparator_1_eq, comparator_2_eq);
  and and_4 (and_4_out, pop, push);
  or or_3 (ERROR, and_3_out, and_4_out);
  Multiplexer #(.width(12), .enable("false")) multiplexer_2 (
    .in0(top), .in1({12{1'b0}}), .out(Top_of_stack), .sel(pop_or_push));
  or or_4 (pop_or_push_or_reset, reset, pop, push);
  or or_5 (pop_or_push, pop, push);
endmodule

// counter add
module add_counter (
  input  [11:0] data,
  input  C,
  output [11:0] S
);

  wire comparator_1_eq, comparator_1_lt, or_1_out;
  wire [11:0] add_1_out_3, bit_extender_1_out;

  assign bit_extender_1_out = {{11{1'b0}}, 1'b1};  // Bit_Extender bit_extender_1
  Comparator #(.width(12)) comparator_1 (.a(data), .b(S), .eq(comparator_1_eq), .lt(comparator_1_lt));  // open: gt
  add add_1 (.in_1(S), .in_2(bit_extender_1_out), .out_3(add_1_out_3));  // open: OF
  or or_1 (or_1_out, comparator_1_eq, comparator_1_lt);
  register_file register_file_1 (
    .S(S), .data(add_1_out_3), .rd(3'b000), .write(1'b1), .reset(or_1_out), .C(C), .rs(3'b000));  // open: T, rt
endmodule

module counter_zonder_stop (
  input  [1:0] in_1,
  input  Reset,
  input  C,
  output [11:0] S
);

  wire [11:0] add_1_out_3, bit_extender_1_out, multiplexer_1_out, register_file_rising_edge_1_s, S_t,
       sub_1_out_3;

  assign bit_extender_1_out = {{11{1'b0}}, 1'b1};  // Bit_Extender bit_extender_1
  add add_1 (.in_1(S_t), .in_2(bit_extender_1_out), .out_3(add_1_out_3));  // open: OF
  sub sub_1 (.in_1(S_t), .in_2(bit_extender_1_out), .out_3(sub_1_out_3));  // open: OF
  Multiplexer #(.select(2), .width(12), .enable("false")) multiplexer_1 (
    .in0({12{1'b0}}), .in1(add_1_out_3), .in2(sub_1_out_3), .out(multiplexer_1_out), .sel(in_1));  // open: in3
  register_file_rising_edge register_file_rising_edge_1 (
    .S(register_file_rising_edge_1_s), .data(multiplexer_1_out), .rd(3'b000), .write(1'b1), .reset(Reset),
    .C(C), .rs(3'b000));  // open: T, rt
  register_file register_file_1 (
    .S(S_t), .data(multiplexer_1_out), .rd(3'b000), .write(1'b1), .reset(Reset), .C(C), .rs(3'b000));  // open: T, rt
  Multiplexer #(.select(2), .width(12), .enable("false")) multiplexer_2 (
    .in0(register_file_rising_edge_1_s), .in1(register_file_rising_edge_1_s), .in2(S_t), .out(S), .sel(in_1));  // open: in3
endmodule

module rising_edge (
  input  C,
  input  write,
  input  reset,
  input  [11:0] D,
  output [11:0] out_5
);

  wire and_1_out;

  D_Flip_Flop d_ff_1 (.clk(and_1_out), .D(D[0]), .Q(out_5[0]), .reset(reset));  // open: Qn, preset, en
  D_Flip_Flop d_ff_2 (.clk(and_1_out), .D(D[1]), .Q(out_5[1]), .reset(reset));  // open: Qn, preset, en
  D_Flip_Flop d_ff_3 (.clk(and_1_out), .D(D[2]), .Q(out_5[2]), .reset(reset));  // open: Qn, preset, en
  D_Flip_Flop d_ff_4 (.clk(and_1_out), .D(D[3]), .Q(out_5[3]), .reset(reset));  // open: Qn, preset, en
  D_Flip_Flop d_ff_5 (.clk(and_1_out), .D(D[4]), .Q(out_5[4]), .reset(reset));  // open: Qn, preset, en
  and and_1 (and_1_out, C, write);
  D_Flip_Flop d_ff_6 (.clk(and_1_out), .D(D[5]), .Q(out_5[5]), .reset(reset));  // open: Qn, preset, en
  D_Flip_Flop d_ff_7 (.clk(and_1_out), .D(D[6]), .Q(out_5[6]), .reset(reset));  // open: Qn, preset, en
  D_Flip_Flop d_ff_8 (.clk(and_1_out), .D(D[7]), .Q(out_5[7]), .reset(reset));  // open: Qn, preset, en
  D_Flip_Flop d_ff_9 (.clk(and_1_out), .D(D[8]), .Q(out_5[8]), .reset(reset));  // open: Qn, preset, en
  D_Flip_Flop d_ff_10 (.clk(and_1_out), .D(D[10]), .Q(out_5[10]), .reset(reset));  // open: Qn, preset, en
  D_Flip_Flop d_ff_11 (.clk(and_1_out), .D(D[9]), .Q(out_5[9]), .reset(reset));  // open: Qn, preset, en
  D_Flip_Flop d_ff_12 (.clk(and_1_out), .D(D[11]), .Q(out_5[11]), .reset(reset));  // open: Qn, preset, en
endmodule

// risign edge reg
module register_file_rising_edge (
  input  [11:0] data,
  input  [2:0] rd,
  input  write,
  input  reset,
  input  C,
  input  [2:0] rs,
  input  [2:0] rt,
  output [11:0] S,
  output [11:0] T
);

  wire [11:0] demultiplexer_1_out0, demultiplexer_1_out1, demultiplexer_1_out2, demultiplexer_1_out3,
       demultiplexer_1_out4, demultiplexer_1_out5, demultiplexer_1_out6, demultiplexer_1_out7, main_1_out_5,
       main_2_out_5, main_3_out_5, main_4_out_5, main_5_out_5, main_6_out_5, main_7_out_5,
       rising_edge_1_out_5;

  Demultiplexer #(.select(3), .width(12), .enable("false")) demultiplexer_1 (
    .out0(demultiplexer_1_out0), .out1(demultiplexer_1_out1), .out2(demultiplexer_1_out2),
    .out3(demultiplexer_1_out3), .out4(demultiplexer_1_out4), .out5(demultiplexer_1_out5),
    .out6(demultiplexer_1_out6), .out7(demultiplexer_1_out7), .in(data), .sel(rd));
  rising_edge rising_edge_1 (
    .C(C), .reset(reset), .D(demultiplexer_1_out0), .write(write), .out_5(rising_edge_1_out_5));
  main main_1 (.reset(reset), .D(demultiplexer_1_out1), .write(write), .out_5(main_1_out_5), .C(C));
  main main_2 (.reset(reset), .D(demultiplexer_1_out2), .write(write), .out_5(main_2_out_5), .C(C));
  main main_3 (.reset(reset), .D(demultiplexer_1_out3), .write(write), .out_5(main_3_out_5), .C(C));
  main main_4 (.reset(reset), .D(demultiplexer_1_out4), .write(write), .out_5(main_4_out_5), .C(C));
  main main_5 (.reset(reset), .D(demultiplexer_1_out5), .write(write), .out_5(main_5_out_5), .C(C));
  main main_6 (.reset(reset), .D(demultiplexer_1_out6), .write(write), .out_5(main_6_out_5), .C(C));
  main main_7 (.reset(reset), .D(demultiplexer_1_out7), .write(write), .out_5(main_7_out_5), .C(C));
  Multiplexer #(.select(3), .width(12), .enable("false")) multiplexer_1 (
    .in0(rising_edge_1_out_5), .in1(main_1_out_5), .in2(main_2_out_5), .in3(main_3_out_5),
    .in4(main_4_out_5), .in5(main_5_out_5), .in6(main_6_out_5), .in7(main_7_out_5), .out(S), .sel(rs));
  Multiplexer #(.select(3), .width(12), .enable("false")) multiplexer_2 (
    .in0(rising_edge_1_out_5), .in1(main_1_out_5), .in2(main_2_out_5), .in3(main_3_out_5),
    .in4(main_4_out_5), .in5(main_5_out_5), .in6(main_6_out_5), .in7(main_7_out_5), .out(T), .sel(rt));
endmodule
