// Logisim project Opgave1.circ as structural Verilog: 1 circuit, main circuit main
module main (
  input  reset,
  input  clock,
  input  [11:0] in_3,
  input  write
);

  wire and_1_out, and_2_out, and_3_out, and_5_out, and_6_out, and_7_out, and_8_out, and_9_out, and_10_out,
       and_11_out, and_12_out;

  D_Flip_Flop #(.trigger("falling")) d_ff_1 (.clk(clock));  // open: D, Q, Qn, preset, en, reset
  and and_1 (and_1_out, in_3[0], write);
  and and_2 (and_2_out, in_3[0], write);
  D_Flip_Flop #(.trigger("falling")) d_ff_2 (.clk(clock));  // open: D, Q, Qn, preset, en, reset
  D_Flip_Flop #(.trigger("falling")) d_ff_3 (.clk(clock));  // open: D, Q, Qn, preset, en, reset
  and and_3 (and_3_out, in_3[0], write);
  D_Flip_Flop #(.trigger("falling")) d_ff_4 (.clk(clock));  // open: D, Q, Qn, preset, en, reset
  // AND_Gate and_4 has open pins: in0=in_3[0], in1=write, out=open
  D_Flip_Flop #(.trigger("falling")) d_ff_5 (.clk(clock));  // open: D, Q, Qn, preset, en, reset
  and and_5 (and_5_out, in_3[0], write);
  and and_6 (and_6_out, in_3[0], write);
  D_Flip_Flop #(.trigger("falling")) d_ff_6 (.clk(clock));  // open: D, Q, Qn, preset, en, reset
  D_Flip_Flop #(.trigger("falling")) d_ff_7 (.clk(clock));  // open: D, Q, Qn, preset, en, reset
  and and_7 (and_7_out, in_3[0], write);
  D_Flip_Flop #(.trigger("falling")) d_ff_8 (.clk(clock));  // open: D, Q, Qn, preset, en, reset
  and and_8 (and_8_out, in_3[0], write);
  D_Flip_Flop #(.trigger("falling")) d_ff_9 (.clk(clock));  // open: D, Q, Qn, preset, en, reset
  and and_9 (and_9_out, in_3[0], write);
  and and_10 (and_10_out, in_3[0], write);
  D_Flip_Flop #(.trigger("falling")) d_ff_10 (.clk(clock));  // open: D, Q, Qn, preset, en, reset
  D_Flip_Flop #(.trigger("falling")) d_ff_11 (.clk(clock));  // open: D, Q, Qn, preset, en, reset
  and and_11 (and_11_out, in_3[0], write);
  D_Flip_Flop #(.trigger("falling")) d_ff_12 (.clk(clock));  // open: D, Q, Qn, preset, en, reset
  and and_12 (and_12_out, in_3[0], write);

  // Notes on the sheet:
  //   ==> alle flipflop states in splitter
  //   ook reset met alles connecteren
  //   AND GATE met clock en write zodat we writen alleen wanneer de clock 1 is, maar eig alleen wnr de clock 0 is omdat falling edge
endmodule
