// Logisim project Opdracht 4.3-4.4.circ as structural Verilog: 4 circuits, main circuit main
module main (
  input  C,
  input  write,
  input  reset,
  input  [11:0] D,
  output [11:0] out_5
);

  wire and_1_out;

  D_Flip_Flop #(.trigger("falling")) d_ff_1 (
    .clk(and_1_out), .D(D[0]), .Q(out_5[0]), .reset(reset));  // open: Qn, preset, en
  D_Flip_Flop #(.trigger("falling")) d_ff_2 (
    .clk(and_1_out), .D(D[1]), .Q(out_5[1]), .reset(reset));  // open: Qn, preset, en
  D_Flip_Flop #(.trigger("falling")) d_ff_3 (
    .clk(and_1_out), .D(D[2]), .Q(out_5[2]), .reset(reset));  // open: Qn, preset, en
  D_Flip_Flop #(.trigger("falling")) d_ff_4 (
    .clk(and_1_out), .D(D[3]), .Q(out_5[3]), .reset(reset));  // open: Qn, preset, en
  D_Flip_Flop #(.trigger("falling")) d_ff_5 (
    .clk(and_1_out), .D(D[4]), .Q(out_5[4]), .reset(reset));  // open: Qn, preset, en
  and and_1 (and_1_out, C, write);
  D_Flip_Flop #(.trigger("falling")) d_ff_6 (
    .clk(and_1_out), .D(D[5]), .Q(out_5[5]), .reset(reset));  // open: Qn, preset, en
  D_Flip_Flop #(.trigger("falling")) d_ff_7 (
    .clk(and_1_out), .D(D[6]), .Q(out_5[6]), .reset(reset));  // open: Qn, preset, en
  D_Flip_Flop #(.trigger("falling")) d_ff_8 (
    .clk(and_1_out), .D(D[7]), .Q(out_5[7]), .reset(reset));  // open: Qn, preset, en
  D_Flip_Flop #(.trigger("falling")) d_ff_9 (
    .clk(and_1_out), .D(D[8]), .Q(out_5[8]), .reset(reset));  // open: Qn, preset, en
  D_Flip_Flop #(.trigger("falling")) d_ff_10 (
    .clk(and_1_out), .D(D[10]), .Q(out_5[10]), .reset(reset));  // open: Qn, preset, en
  D_Flip_Flop #(.trigger("falling")) d_ff_11 (
    .clk(and_1_out), .D(D[9]), .Q(out_5[9]), .reset(reset));  // open: Qn, preset, en
  D_Flip_Flop #(.trigger("falling")) d_ff_12 (
    .clk(and_1_out), .D(D[11]), .Q(out_5[11]), .reset(reset));  // open: Qn, preset, en
endmodule

module register_file (
  input  [11:0] data,
  input  [2:0] rd,
  input  write,
  input  reset,
  input  C,
  input  [2:0] rs,
  input  [2:0] rt,
  output [11:0] S,
  output [11:0] T
);

  wire demultiplexer_1_out0, demultiplexer_1_out1, demultiplexer_1_out2, demultiplexer_1_out3,
       demultiplexer_1_out4, demultiplexer_1_out5, demultiplexer_1_out6, demultiplexer_1_out7;
  wire [11:0] main_1_out_5, main_2_out_5, main_3_out_5, main_4_out_5, main_5_out_5, main_6_out_5,
       main_7_out_5, main_8_out_5;

  Demultiplexer #(.select(3), .enable("false")) demultiplexer_1 (
    .out0(demultiplexer_1_out0), .out1(demultiplexer_1_out1), .out2(demultiplexer_1_out2),
    .out3(demultiplexer_1_out3), .out4(demultiplexer_1_out4), .out5(demultiplexer_1_out5),
    .out6(demultiplexer_1_out6), .out7(demultiplexer_1_out7), .in(write), .sel(rd));
  main main_1 (.reset(reset), .D({12{1'b0}}), .write(demultiplexer_1_out0), .out_5(main_1_out_5), .C(C));
  main main_2 (.reset(reset), .D(data), .write(demultiplexer_1_out1), .out_5(main_2_out_5), .C(C));
  main main_3 (.reset(reset), .D(data), .write(demultiplexer_1_out2), .out_5(main_3_out_5), .C(C));
  main main_4 (.reset(reset), .D(data), .write(demultiplexer_1_out3), .out_5(main_4_out_5), .C(C));
  main main_5 (.reset(reset), .D(data), .write(demultiplexer_1_out4), .out_5(main_5_out_5), .C(C));
  main main_6 (.reset(reset), .D(data), .write(demultiplexer_1_out5), .out_5(main_6_out_5), .C(C));
  main main_7 (.reset(reset), .D(data), .write(demultiplexer_1_out6), .out_5(main_7_out_5), .C(C));
  main main_8 (.reset(reset), .D(data), .write(demultiplexer_1_out7), .out_5(main_8_out_5), .C(C));
  Multiplexer #(.select(3), .width(12), .enable("false")) multiplexer_1 (
    .in0(main_1_out_5), .in1(main_2_out_5), .in2(main_3_out_5), .in3(main_4_out_5), .in4(main_5_out_5),
    .in5(main_6_out_5), .in6(main_7_out_5), .in7(main_8_out_5), .out(S), .sel(rs));
  Multiplexer #(.select(3), .width(12), .enable("false")) multiplexer_2 (
    .in0(main_1_out_5), .in1(main_2_out_5), .in2(main_3_out_5), .in3(main_4_out_5), .in4(main_5_out_5),
    .in5(main_6_out_5), .in6(main_7_out_5), .in7(main_8_out_5), .out(T), .sel(rt));
endmodule

module counter (
  input  [11:0] data,
  input  write,
  input  C,
  output [11:0] S
);

  wire comparator_1_eq, comparator_1_lt, or_1_out;
  wire [11:0] add_1_out_3, bit_extender_1_out;

  assign bit_extender_1_out = {{11{1'b0}}, 1'b1};  // Bit_Extender bit_extender_1
  Comparator #(.width(12)) comparator_1 (.a(data), .b(S), .eq(comparator_1_eq), .lt(comparator_1_lt));  // open: gt
  add add_1 (.in_1(S), .in_2(bit_extender_1_out), .out_3(add_1_out_3));  // open: OF
  or or_1 (or_1_out, comparator_1_eq, comparator_1_lt);
  register_file register_file_1 (
    .S(S), .data(add_1_out_3), .rd(3'b001), .write(write), .reset(or_1_out), .C(C), .rs(3'b001));  // open: T, rt
endmodule

module finite_state_machine (
);

  wire and_1_out, and_2_out, and_3_out, and_4_out, clock_1_out, comparator_1_eq, comparator_1_gt,
       comparator_1_lt, comparator_2_eq, comparator_2_gt, comparator_2_lt, comparator_3_eq, comparator_3_gt,
       comparator_4_eq, comparator_4_gt, comparator_4_lt, comparator_5_eq, comparator_5_gt, comparator_5_lt,
       comparator_6_eq, comparator_6_gt, comparator_6_lt, or_1_out, or_2_out, or_3_out, or_4_out, or_5_out,
       or_6_out, or_7_out;
  wire [11:0] counter_1_s;

  Clock clock_1 (.out(clock_1_out));
  // Probe on 12'h1c
  counter counter_1 (.data(12'h1c), .write(1'b1), .C(clock_1_out), .S(counter_1_s));
  // Probe on counter_1_s
  // Probe on 12'h8
  // Probe on 12'hc
  // Probe on 12'h1c
  // Probe on 12'he
  // Probe on 12'h16
  // Probe on 12'h1a
  Comparator #(.width(12)) comparator_1 (
    .a(12'h8), .b(counter_1_s), .gt(comparator_1_gt), .eq(comparator_1_eq), .lt(comparator_1_lt));
  Comparator #(.width(12)) comparator_2 (
    .a(12'hc), .b(counter_1_s), .gt(comparator_2_gt), .eq(comparator_2_eq), .lt(comparator_2_lt));
  Comparator #(.width(12)) comparator_3 (
    .a(12'h1c), .b(counter_1_s), .gt(comparator_3_gt), .eq(comparator_3_eq));  // open: lt
  Comparator #(.width(12)) comparator_4 (
    .a(12'he), .b(counter_1_s), .gt(comparator_4_gt), .eq(comparator_4_eq), .lt(comparator_4_lt));
  Comparator #(.width(12)) comparator_5 (
    .a(12'h16), .b(counter_1_s), .gt(comparator_5_gt), .eq(comparator_5_eq), .lt(comparator_5_lt));
  Comparator #(.width(12)) comparator_6 (
    .a(12'h1a), .b(counter_1_s), .gt(comparator_6_gt), .eq(comparator_6_eq), .lt(comparator_6_lt));
  or or_1 (or_1_out, comparator_1_gt, comparator_1_eq);
  and and_1 (and_1_out, comparator_1_lt, or_2_out);
  or or_2 (or_2_out, comparator_2_gt, comparator_2_eq);
  and and_2 (and_2_out, comparator_2_lt, or_3_out);
  or or_3 (or_3_out, comparator_3_gt, comparator_3_eq);
  or or_4 (or_4_out, comparator_4_gt, comparator_4_eq);
  and and_3 (and_3_out, comparator_4_lt, or_5_out);
  or or_5 (or_5_out, comparator_5_gt, comparator_5_eq);
  and and_4 (and_4_out, comparator_5_lt, or_6_out);
  or or_6 (or_6_out, comparator_6_gt, comparator_6_eq);
  LED led_1 (.in(and_2_out));
  LED led_2 (.in(and_1_out));
  LED led_3 (.in(or_1_out));
  or or_7 (or_7_out, or_4_out, comparator_6_lt);
  LED led_4 (.in(or_7_out));
  LED led_5 (.in(and_4_out));
  LED led_6 (.in(and_3_out));
endmodule
