// Logisim project SD_Group69.circ as structural Verilog: 8 circuits, main circuit main
module main (
  output [11:0] pc,
  output [11:0] r0,
  output [11:0] r1,
  output [11:0] r2,
  output [11:0] r3,
  output [11:0] r4,
  output [11:0] r5,
  output [11:0] r6,
  output [11:0] r7,
  output halt
);

  wire clock, clock_1_out, controller_1_lui, controller_1_lw, controller_1_sw, not_1_out, or_1_out, reset;
  wire [2:0] decoder_1_operation, decoder_1_rd, decoder_1_rs, decoder_1_rt, rd, rs, rt;
  wire [3:0] decoder_1_funct, Function;
  wire [11:0] controller_1_immediate, multiplexer_1_out, multiplexer_2_out, n12_bit_alu_1_result, ram_2_data,
       register_1_s, register_1_t;
  wire [15:0] ram_1_data;

  Halt halt_1 (.instruction(ram_1_data), .clock(clock_1_out), .reset(reset), .halt(halt));
  Clock clock_1 (.out(clock_1_out));
  Button u_reset (.out(reset));
  and and_1 (clock, ~halt, clock_1_out);  // AND_Gate
  _12_bit_program_counter u_12_bit_program_counter_1 (
    .branch_relative(1'b0), .branch_absolute(1'b0), .branch_value({12{1'b0}}), .clock(clock), .reset(reset),
    .instruction_adress(pc));
  // Probe on ram_1_data
  RAM #(.addrWidth(12), .dataWidth(16)) ram_1 (
    .addr(pc), .data(ram_1_data), .clk(clock), .ld(1'b1), .clr(reset));  // open: sel
  Decoder decoder_1 (
    .in_1(ram_1_data), .operation(decoder_1_operation), .rd(decoder_1_rd), .rs(decoder_1_rs),
    .rt(decoder_1_rt), .funct(decoder_1_funct));
  Controller controller_1 (
    .operation(decoder_1_operation), .rd(decoder_1_rd), .rs(decoder_1_rs), .rt(decoder_1_rt),
    .\function (decoder_1_funct), .rd_2(rd), .rs_2(rt), .rt_2(rs), .funct(Function),
    .immediate(controller_1_immediate), .sw(controller_1_sw), .lw(controller_1_lw), .lui(controller_1_lui));
  not not_1 (not_1_out, controller_1_sw);
  register register_1 (
    .data(multiplexer_2_out), .S(register_1_s), .T(register_1_t), .rd(rd), .write(not_1_out), .reset(reset),
    .C(clock), .out_8(r0), .out_9(r1), .out_10(r2), .out_11(r3), .out_12(r4), .out_13(r5), .out_14(r6),
    .out_15(r7), .rs(rs), .rt(rt));
  // Probe on register_1_t
  _12_bit_ALU u_12_bit_alu_1 (
    .ALU_code(Function), .a(register_1_t), .b(multiplexer_1_out), .result(n12_bit_alu_1_result));  // open: overflow
  Multiplexer #(.width(12), .enable("false")) multiplexer_1 (
    .in0(register_1_s), .in1(controller_1_immediate), .out(multiplexer_1_out), .sel(or_1_out));
  Multiplexer #(.width(12), .enable("false")) multiplexer_2 (
    .in0(n12_bit_alu_1_result), .in1(ram_2_data), .out(multiplexer_2_out), .sel(controller_1_lw));
  or or_1 (or_1_out, controller_1_sw, controller_1_lui, controller_1_lw);
  // Probe on n12_bit_alu_1_result
  RAM #(.addrWidth(12), .dataWidth(12), .bus("separate")) ram_2 (
    .addr(n12_bit_alu_1_result), .din(register_1_t), .data(ram_2_data), .str(controller_1_sw), .clk(clock),
    .ld(controller_1_lw), .clr(reset));  // open: sel
  // Probe on ram_2_data

  // Notes on the sheet:
  //   current instruction
  //   clock signal
  //   reset button
  //   sw
  //   lw
  //   DO NOT CHANGE THE INPUTS AND OUTPUTS OF THIS CIRCUIT! Do not add/remove inputs or outputs. Do not even change their location or orientation.
endmodule

module Halt (
  input  [15:0] instruction,
  input  clock,
  input  reset,
  output halt
);

  wire and_1_out, comparator_1_eq, comparator_2_gt, counter_1_carry, or_1_out, or_2_out;
  wire [11:0] counter_1_q;

  Comparator #(.width(16), .mode("unsigned")) comparator_1 (
    .a(instruction), .b({16{1'b0}}), .eq(comparator_1_eq));  // open: gt, lt
  Counter #(.width(12), .max('hfff), .trigger("falling")) counter_1 (
    .Q(counter_1_q), .carry(counter_1_carry), .clk(clock), .clr(reset));  // open: load, D, count
  or or_1 (or_1_out, comparator_1_eq, counter_1_carry);
  Comparator #(.width(12), .mode("unsigned")) comparator_2 (
    .a(counter_1_q), .b({12{1'b0}}), .gt(comparator_2_gt));  // open: eq, lt
  or or_2 (or_2_out, halt, and_1_out);
  and and_1 (and_1_out, or_1_out, comparator_2_gt);
  Register #(.width(1)) register_1 (.D(or_2_out), .Q(halt), .clk(clock), .clr(reset));  // open: en

  // Notes on the sheet:
  //   halt becomes and stays asserted if the instruction is 0000 (not in the first clock cycle) or the end of the counter is reached (2^12)
endmodule

module _12_bit_program_counter (
  input  branch_relative,
  input  branch_absolute,
  input  [11:0] branch_value,
  input  clock,
  input  reset,
  output [11:0] instruction_adress
);

  wire xnor_1_out;
  wire [1:0] controlled_buffer_1_out;

  counter_for_pc counter_for_pc_1 (
    .in_4(branch_value), .in_3(controlled_buffer_1_out), .Reset(reset), .C(clock), .S(instruction_adress));
  xnor xnor_1 (xnor_1_out, branch_absolute, branch_relative);
  assign controlled_buffer_1_out = xnor_1_out ? 2'b00 : 2'bz;  // Controlled_Buffer controlled_buffer_1
  assign controlled_buffer_1_out = branch_absolute ? 2'b01 : 2'bz;  // Controlled_Buffer controlled_buffer_2
  assign controlled_buffer_1_out = branch_relative ? 2'b10 : 2'bz;  // Controlled_Buffer controlled_buffer_3
endmodule

module counter_for_pc (
  input  Reset,
  input  C,
  input  [1:0] in_3,
  input  [11:0] in_4,
  output [11:0] S
);

  wire [11:0] add_1_out_3, add_2_out_3, add_3_out_3, bit_extender_1_out, bit_extender_2_out,
       multiplexer_1_out;

  assign bit_extender_1_out = {{11{1'b0}}, 1'b1};  // Bit_Extender bit_extender_1
  assign bit_extender_2_out = {{11{1'b0}}, 1'b1};  // Bit_Extender bit_extender_2
  add add_1 (.in_1(S), .in_2(bit_extender_1_out), .out_3(add_1_out_3));  // open: OF
  add add_2 (.in_1(in_4), .in_2(add_3_out_3), .out_3(add_2_out_3));  // open: OF
  add add_3 (.in_1(S), .in_2(bit_extender_2_out), .out_3(add_3_out_3));  // open: OF
  Multiplexer #(.select(2), .width(12), .enable("false")) multiplexer_1 (
    .in0(add_1_out_3), .in1(in_4), .in2(add_2_out_3), .out(multiplexer_1_out), .sel(in_3));  // open: in3
  register register_1 (
    .data(multiplexer_1_out), .T(S), .rd(3'b001), .write(1'b1), .reset(Reset), .C(C), .rs(3'b001), .rt(3'b001));  // open: S, out_8, out_9, out_10, out_11, out_12, out_13, out_14, out_15
endmodule

module klein_reg (
  input  C,
  input  write,
  input  reset,
  input  [11:0] D,
  output [11:0] out_5
);

  wire and_1_out;

  D_Flip_Flop d_ff_1 (.clk(and_1_out), .D(D[0]), .Q(out_5[0]), .reset(reset));  // open: Qn, preset, en
  D_Flip_Flop d_ff_2 (.clk(and_1_out), .D(D[1]), .Q(out_5[1]), .reset(reset));  // open: Qn, preset, en
  D_Flip_Flop d_ff_3 (.clk(and_1_out), .D(D[2]), .Q(out_5[2]), .reset(reset));  // open: Qn, preset, en
  D_Flip_Flop d_ff_4 (.clk(and_1_out), .D(D[3]), .Q(out_5[3]), .reset(reset));  // open: Qn, preset, en
  D_Flip_Flop d_ff_5 (.clk(and_1_out), .D(D[4]), .Q(out_5[4]), .reset(reset));  // open: Qn, preset, en
  and and_1 (and_1_out, C, write);
  D_Flip_Flop d_ff_6 (.clk(and_1_out), .D(D[5]), .Q(out_5[5]), .reset(reset));  // open: Qn, preset, en
  D_Flip_Flop d_ff_7 (.clk(and_1_out), .D(D[6]), .Q(out_5[6]), .reset(reset));  // open: Qn, preset, en
  D_Flip_Flop d_ff_8 (.clk(and_1_out), .D(D[7]), .Q(out_5[7]), .reset(reset));  // open: Qn, preset, en
  D_Flip_Flop d_ff_9 (.clk(and_1_out), .D(D[8]), .Q(out_5[8]), .reset(reset));  // open: Qn, preset, en
  D_Flip_Flop d_ff_10 (.clk(and_1_out), .D(D[10]), .Q(out_5[10]), .reset(reset));  // open: Qn, preset, en
  D_Flip_Flop d_ff_11 (.clk(and_1_out), .D(D[9]), .Q(out_5[9]), .reset(reset));  // open: Qn, preset, en
  D_Flip_Flop d_ff_12 (.clk(and_1_out), .D(D[11]), .Q(out_5[11]), .reset(reset));  // open: Qn, preset, en
endmodule

module register (
  input  write,
  input  [2:0] rd,
  input  reset,
  input  C,
  input  [2:0] rs,
  input  [11:0] data,
  input  [2:0] rt,
  output [11:0] out_8,
  output [11:0] out_9,
  output [11:0] out_10,
  output [11:0] out_11,
  output [11:0] out_12,
  output [11:0] out_13,
  output [11:0] out_14,
  output [11:0] out_15,
  output [11:0] S,
  output [11:0] T
);

  wire demultiplexer_1_out0, demultiplexer_1_out1, demultiplexer_1_out2, demultiplexer_1_out3,
       demultiplexer_1_out4, demultiplexer_1_out5, demultiplexer_1_out6, demultiplexer_1_out7;

  Demultiplexer #(.select(3), .enable("false")) demultiplexer_1 (
    .out0(demultiplexer_1_out0), .out1(demultiplexer_1_out1), .out2(demultiplexer_1_out2),
    .out3(demultiplexer_1_out3), .out4(demultiplexer_1_out4), .out5(demultiplexer_1_out5),
    .out6(demultiplexer_1_out6), .out7(demultiplexer_1_out7), .in(write), .sel(rd));
  Opdracht_4_3_4_4_main main_1 (.reset(reset), .D({12{1'b0}}), .write(demultiplexer_1_out0), .out_5(out_8), .C(C));
  Opdracht_4_3_4_4_main main_2 (.reset(reset), .D(data), .write(demultiplexer_1_out1), .out_5(out_9), .C(C));
  Opdracht_4_3_4_4_main main_3 (.reset(reset), .D(data), .write(demultiplexer_1_out2), .out_5(out_10), .C(C));
  Opdracht_4_3_4_4_main main_4 (.reset(reset), .D(data), .write(demultiplexer_1_out3), .out_5(out_11), .C(C));
  Opdracht_4_3_4_4_main main_5 (.reset(reset), .D(data), .write(demultiplexer_1_out4), .out_5(out_12), .C(C));
  Opdracht_4_3_4_4_main main_6 (.reset(reset), .D(data), .write(demultiplexer_1_out5), .out_5(out_13), .C(C));
  Opdracht_4_3_4_4_main main_7 (.reset(reset), .D(data), .write(demultiplexer_1_out6), .out_5(out_14), .C(C));
  Opdracht_4_3_4_4_main main_8 (.reset(reset), .D(data), .write(demultiplexer_1_out7), .out_5(out_15), .C(C));
  Multiplexer #(.select(3), .width(12), .enable("false")) multiplexer_1 (
    .in0(out_8), .in1(out_9), .in2(out_10), .in3(out_11), .in4(out_12), .in5(out_13), .in6(out_14),
    .in7(out_15), .out(S), .sel(rs));
  Multiplexer #(.select(3), .width(12), .enable("false")) multiplexer_2 (
    .in0(out_8), .in1(out_9), .in2(out_10), .in3(out_11), .in4(out_12), .in5(out_13), .in6(out_14),
    .in7(out_15), .out(T), .sel(rt));
endmodule

module Decoder (
  input  [15:0] in_1,
  output [2:0] operation,
  output [2:0] rd,
  output [2:0] rs,
  output [2:0] rt,
  output [3:0] funct
);


  assign funct = in_1[3:0];
  assign operation = in_1[15:13];
  assign rd = in_1[12:10];
  assign rs = in_1[9:7];
  assign rt = in_1[6:4];
endmodule

module Controller (
  input  [2:0] operation,
  input  [2:0] rd,
  input  [2:0] rs,
  input  [2:0] rt,
  input  [3:0] \function ,
  output [2:0] rd_2,
  output [2:0] rs_2,
  output [2:0] rt_2,
  output [3:0] funct,
  output sw,
  output lw,
  output [11:0] immediate,
  output lui
);

  wire addi, comparator_1_eq, comparator_2_eq, comparator_3_eq, ldi, lui_t, not_1_out, not_2_out, not_3_out,
       subi;
  wire [3:0] multiplexer_1_out, n4_bit_adder_1_sum_0_1_2_3;
  wire [11:0] bit_extender_1_out, bit_extender_2_out, bit_extender_3_out, controlled_buffer_1_out;

  Multiplexer #(.width(4), .enable("false")) multiplexer_1 (
    .in0(4'b0000), .in1(4'b0001), .out(multiplexer_1_out), .sel(subi));
  Comparator #(.width(3)) comparator_1 (.a(operation), .b(3'b111), .eq(comparator_1_eq));  // open: gt, lt
  Comparator #(.width(3)) comparator_2 (.a(operation), .b(3'b100), .eq(comparator_2_eq));  // open: gt, lt
  Comparator #(.width(3)) comparator_3 (.a(operation), .b(3'b011), .eq(comparator_3_eq));  // open: gt, lt
  _4_Bit_Adder u_4_bit_adder_1 (
    .Carry_in(1'b0), .A(\function ), .B(4'b1000), .SUM_0_1_2_3(n4_bit_adder_1_sum_0_1_2_3));  // open: P0, G0
  Multiplexer #(.select(3), .width(3), .enable("false")) multiplexer_2 (
    .in0(3'b000), .in1(rs), .in2(rs), .in3(3'b000), .in4(rd), .in5(rs), .in6(3'b000), .in7(rs), .out(rs_2),
    .sel(operation));
  Multiplexer #(.select(3), .width(3), .enable("false")) multiplexer_3 (
    .in0(3'b000), .in1(rt), .in2(3'b000), .in3(3'b000), .in4(3'b000), .in5(3'b000), .in6(3'b000),
    .in7(3'b000), .out(rt_2), .sel(operation));
  Multiplexer #(.select(3), .width(4), .enable("false")) multiplexer_4 (
    .in0(\function ), .in1(\function ), .in2(n4_bit_adder_1_sum_0_1_2_3), .in3(4'b0000),
    .in4(multiplexer_1_out), .in5(\function ), .in6(\function ), .in7(4'b0000), .out(funct), .sel(operation));
  and u_sw (sw, \function [0], comparator_1_eq);
  not not_1 (not_1_out, \function [0]);
  and u_lw (lw, not_1_out, comparator_1_eq);
  and u_subi (subi, \function [0], comparator_2_eq);
  not not_2 (not_2_out, \function [0]);
  and u_addi (addi, not_2_out, comparator_2_eq);
  and u_lui (lui_t, \function [0], comparator_3_eq);
  not not_3 (not_3_out, \function [0]);
  and u_ldi (ldi, not_3_out, comparator_3_eq);
  or or_1 (lui, subi, addi, lui_t, ldi);
  assign bit_extender_1_out = {{3{1'b0}}, {rs, rt, \function [3:1]}};  // Bit_Extender bit_extender_1
  assign controlled_buffer_1_out = ldi ? bit_extender_2_out : 12'bz;  // Controlled_Buffer controlled_buffer_1
  assign bit_extender_2_out = {{3{rs[2]}}, {rs, rt, \function [3:1]}};  // Bit_Extender bit_extender_2
  assign controlled_buffer_1_out = lui_t ? {rs, rt, \function [3:1], 3'b000} : 12'bz;  // Controlled_Buffer controlled_buffer_2
  assign bit_extender_3_out = {{6{1'b0}}, {rt, \function [3:1]}};  // Bit_Extender bit_extender_3
  Multiplexer #(.select(3), .width(12), .enable("false")) multiplexer_5 (
    .in3(controlled_buffer_1_out), .in4(bit_extender_1_out), .in7(bit_extender_3_out), .out(immediate),
    .sel(operation));  // open: in0, in1, in2, in5, in6

  assign rd_2 = rd;

  // Other names for the same wires on the sheet: im[2:0] = \function [3:1]

  // Notes on the sheet:
  //   add
endmodule
