// Logisim project FD_Group69.circ as structural Verilog: 8 circuits, main circuit main
module main (
  output [11:0] pc,
  output [11:0] r0,
  output [11:0] r1,
  output [11:0] r2,
  output [11:0] r3,
  output [11:0] r4,
  output [11:0] r5,
  output [11:0] r6,
  output [11:0] r7,
  output halt
);

  wire branch_a, brnz, clock, clock_1_out, comparator_1_eq, controller_1_brnz, controller_1_exceptions,
       controller_1_j, controller_1_jal, controller_1_lui, controller_1_lw, controller_1_sw, halt_1_halt, jr,
       multiplexer_1_out, n12_bit_alu_1_overflow, nand_1_out, not_1_out, not_2_out, or_3_out, reset,
       xor_1_out;
  wire [2:0] decoder_1_operation, decoder_1_rd, decoder_1_rs, decoder_1_rt, rd, rs, rt;
  wire [3:0] decoder_1_funct, Function;
  wire [11:0] add_1_out_3, controller_1_immediate, multiplexer_2_out, multiplexer_4_out, multiplexer_5_out,
       multiplexer_6_out, n12_bit_alu_1_result, ram_2_data, register_1_s, register_1_t;
  wire [15:0] ram_1_data;

  Halt halt_1 (.instruction(ram_1_data), .clock(clock_1_out), .reset(reset), .halt(halt_1_halt));
  Clock clock_1 (.out(clock_1_out));
  Button u_reset (.out(reset));
  and and_1 (clock, ~halt, clock_1_out);  // AND_Gate
  or or_1 (halt, halt_1_halt, controller_1_exceptions, n12_bit_alu_1_overflow);
  _12_bit_program_counter u_12_bit_program_counter_1 (
    .branch_relative(brnz), .branch_absolute(branch_a), .branch_value(multiplexer_2_out), .clock(clock),
    .reset(reset), .instruction_adress(pc));
  Comparator #(.width(12)) comparator_1 (.a(register_1_t), .b({12{1'b0}}), .eq(comparator_1_eq));  // open: gt, lt
  nand nand_1 (nand_1_out, comparator_1_eq, controller_1_brnz);
  Multiplexer #(.enable("false")) multiplexer_1 (
    .in0(nand_1_out), .in1(1'b0), .out(multiplexer_1_out), .sel(not_1_out));
  // Probe on ram_1_data
  Multiplexer #(.width(12), .enable("false")) multiplexer_2 (
    .in0(controller_1_immediate), .in1(n12_bit_alu_1_result), .out(multiplexer_2_out), .sel(jr));
  not not_1 (not_1_out, controller_1_brnz);
  Multiplexer #(.enable("false")) multiplexer_3 (.in0(1'b0), .in1(1'b1), .out(brnz), .sel(multiplexer_1_out));
  RAM #(.addrWidth(12), .dataWidth(16)) ram_1 (.addr(pc), .data(ram_1_data), .clk(clock), .ld(1'b1));  // open: sel, clr
  or or_2 (branch_a, jr, controller_1_j, controller_1_jal);
  Decoder decoder_1 (
    .in_1(ram_1_data), .operation(decoder_1_operation), .rd(decoder_1_rd), .rs(decoder_1_rs),
    .rt(decoder_1_rt), .funct(decoder_1_funct));
  Controller controller_1 (
    .operation(decoder_1_operation), .rd(decoder_1_rd), .rd_2(rd), .rs(decoder_1_rs), .rs_2(rt),
    .rt(decoder_1_rt), .rt_2(rs), .\function (decoder_1_funct), .funct(Function), .sw(controller_1_sw),
    .lw(controller_1_lw), .immediate(controller_1_immediate), .lui(controller_1_lui), .jr(jr),
    .brnz(controller_1_brnz), .jal(controller_1_jal), .j(controller_1_j), .exceptions(controller_1_exceptions));
  Multiplexer #(.width(12), .enable("false")) multiplexer_4 (
    .in0(multiplexer_6_out), .in1(add_1_out_3), .out(multiplexer_4_out), .sel(controller_1_jal));
  ExactlyOne xor_1 (.out(xor_1_out), .in0(not_2_out), .in1(controller_1_j), .in2(jr));
  not not_2 (not_2_out, controller_1_sw);
  add add_1 (.in_1(pc), .in_2(12'h1), .out_3(add_1_out_3));  // open: OF
  register register_1 (
    .data(multiplexer_4_out), .S(register_1_s), .T(register_1_t), .rd(rd), .write(xor_1_out), .reset(reset),
    .C(clock), .out_8(r0), .out_9(r1), .out_10(r2), .out_11(r3), .out_12(r4), .out_13(r5), .out_14(r6),
    .out_15(r7), .rs(rs), .rt(rt));
  // Probe on register_1_t
  _12_bit_ALU u_12_bit_alu_1 (
    .ALU_code(Function), .a(register_1_t), .b(multiplexer_5_out), .overflow(n12_bit_alu_1_overflow),
    .result(n12_bit_alu_1_result));
  Multiplexer #(.width(12), .enable("false")) multiplexer_5 (
    .in0(register_1_s), .in1(controller_1_immediate), .out(multiplexer_5_out), .sel(or_3_out));
  Multiplexer #(.width(12), .enable("false")) multiplexer_6 (
    .in0(n12_bit_alu_1_result), .in1(ram_2_data), .out(multiplexer_6_out), .sel(controller_1_lw));
  or or_3 (or_3_out, controller_1_sw, controller_1_lui, controller_1_lw);
  // Probe on n12_bit_alu_1_result
  RAM #(.addrWidth(12), .dataWidth(12), .bus("separate")) ram_2 (
    .addr(n12_bit_alu_1_result), .din(register_1_s), .data(ram_2_data), .str(controller_1_sw), .clk(clock),
    .ld(controller_1_lw), .clr(reset));  // open: sel
  // Probe on ram_2_data

  // Notes on the sheet:
  //   current instruction
  //   clock signal
  //   reset button
  //   sw
  //   lw
  //   DO NOT CHANGE THE INPUTS AND OUTPUTS OF THIS CIRCUIT! Do not add/remove inputs or outputs. Do not even change their location or orientation.
endmodule

module Halt (
  input  [15:0] instruction,
  input  clock,
  input  reset,
  output halt
);

  wire and_1_out, comparator_1_eq, comparator_2_gt, counter_1_carry, or_1_out, or_2_out;
  wire [11:0] counter_1_q;

  Comparator #(.width(16), .mode("unsigned")) comparator_1 (
    .a(instruction), .b({16{1'b0}}), .eq(comparator_1_eq));  // open: gt, lt
  Counter #(.width(12), .max('hfff), .trigger("falling")) counter_1 (
    .Q(counter_1_q), .carry(counter_1_carry), .clk(clock), .clr(reset));  // open: load, D, count
  or or_1 (or_1_out, comparator_1_eq, counter_1_carry);
  Comparator #(.width(12), .mode("unsigned")) comparator_2 (
    .a(counter_1_q), .b({12{1'b0}}), .gt(comparator_2_gt));  // open: eq, lt
  or or_2 (or_2_out, halt, and_1_out);
  and and_1 (and_1_out, or_1_out, comparator_2_gt);
  Register #(.width(1)) register_1 (.D(or_2_out), .Q(halt), .clk(clock), .clr(reset));  // open: en

  // Notes on the sheet:
  //   halt becomes and stays asserted if the instruction is 0000 (not in the first clock cycle) or the end of the counter is reached (2^12)
endmodule

module _12_bit_program_counter (
  input  branch_relative,
  input  branch_absolute,
  input  [11:0] branch_value,
  input  clock,
  input  reset,
  output [11:0] instruction_adress
);

  wire xnor_1_out;
  wire [1:0] controlled_buffer_1_out;

  counter_for_pc counter_for_pc_1 (
    .in_4(branch_value), .in_3(controlled_buffer_1_out), .Reset(reset), .C(clock), .S(instruction_adress));
  xnor xnor_1 (xnor_1_out, branch_absolute, branch_relative);
  assign controlled_buffer_1_out = xnor_1_out ? 2'b00 : 2'bz;  // Controlled_Buffer controlled_buffer_1
  assign controlled_buffer_1_out = branch_absolute ? 2'b01 : 2'bz;  // Controlled_Buffer controlled_buffer_2
  assign controlled_buffer_1_out = branch_relative ? 2'b10 : 2'bz;  // Controlled_Buffer controlled_buffer_3
endmodule

module counter_for_pc (
  input  Reset,
  input  C,
  input  [1:0] in_3,
  input  [11:0] in_4,
  output [11:0] S
);

  wire [11:0] add_1_out_3, add_2_out_3, add_3_out_3, bit_extender_1_out, bit_extender_2_out,
       multiplexer_1_out;

  assign bit_extender_1_out = {{11{1'b0}}, 1'b1};  // Bit_Extender bit_extender_1
  assign bit_extender_2_out = {{11{1'b0}}, 1'b1};  // Bit_Extender bit_extender_2
  add add_1 (.in_1(S), .in_2(bit_extender_1_out), .out_3(add_1_out_3));  // open: OF
  add add_2 (.in_1(in_4), .in_2(add_3_out_3), .out_3(add_2_out_3));  // open: OF
  add add_3 (.in_1(S), .in_2(bit_extender_2_out), .out_3(add_3_out_3));  // open: OF
  Multiplexer #(.select(2), .width(12), .enable("false")) multiplexer_1 (
    .in0(add_1_out_3), .in1(in_4), .in2(add_2_out_3), .out(multiplexer_1_out), .sel(in_3));  // open: in3
  register register_1 (
    .data(multiplexer_1_out), .T(S), .rd(3'b001), .write(1'b1), .reset(Reset), .C(C), .rs(3'b001), .rt(3'b001));  // open: S, out_8, out_9, out_10, out_11, out_12, out_13, out_14, out_15
endmodule

module klein_reg (
  input  C,
  input  write,
  input  reset,
  input  [11:0] D,
  output [11:0] out_5
);

  wire and_1_out;

  D_Flip_Flop d_ff_1 (.clk(and_1_out), .D(D[0]), .Q(out_5[0]), .reset(reset));  // open: Qn, preset, en
  D_Flip_Flop d_ff_2 (.clk(and_1_out), .D(D[2]), .Q(out_5[2]), .reset(reset));  // open: Qn, preset, en
  D_Flip_Flop d_ff_3 (.clk(and_1_out), .D(D[1]), .Q(out_5[1]), .reset(reset));  // open: Qn, preset, en
  D_Flip_Flop d_ff_4 (.clk(and_1_out), .D(D[3]), .Q(out_5[3]), .reset(reset));  // open: Qn, preset, en
  D_Flip_Flop d_ff_5 (.clk(and_1_out), .D(D[4]), .Q(out_5[4]), .reset(reset));  // open: Qn, preset, en
  and and_1 (and_1_out, C, write);
  D_Flip_Flop d_ff_6 (.clk(and_1_out), .D(D[6]), .Q(out_5[6]), .reset(reset));  // open: Qn, preset, en
  D_Flip_Flop d_ff_7 (.clk(and_1_out), .D(D[5]), .Q(out_5[5]), .reset(reset));  // open: Qn, preset, en
  D_Flip_Flop d_ff_8 (.clk(and_1_out), .D(D[7]), .Q(out_5[7]), .reset(reset));  // open: Qn, preset, en
  D_Flip_Flop d_ff_9 (.clk(and_1_out), .D(D[8]), .Q(out_5[8]), .reset(reset));  // open: Qn, preset, en
  D_Flip_Flop d_ff_10 (.clk(and_1_out), .D(D[9]), .Q(out_5[9]), .reset(reset));  // open: Qn, preset, en
  D_Flip_Flop d_ff_11 (.clk(and_1_out), .D(D[10]), .Q(out_5[10]), .reset(reset));  // open: Qn, preset, en
  D_Flip_Flop d_ff_12 (.clk(and_1_out), .D(D[11]), .Q(out_5[11]), .reset(reset));  // open: Qn, preset, en
endmodule

module register (
  input  write,
  input  [2:0] rd,
  input  reset,
  input  C,
  input  [2:0] rs,
  input  [11:0] data,
  input  [2:0] rt,
  output [11:0] out_8,
  output [11:0] out_9,
  output [11:0] out_10,
  output [11:0] out_11,
  output [11:0] out_12,
  output [11:0] out_13,
  output [11:0] out_14,
  output [11:0] out_15,
  output [11:0] S,
  output [11:0] T
);

  wire demultiplexer_1_out0, demultiplexer_1_out1, demultiplexer_1_out2, demultiplexer_1_out3,
       demultiplexer_1_out4, demultiplexer_1_out5, demultiplexer_1_out6, demultiplexer_1_out7;

  Demultiplexer #(.select(3), .enable("false")) demultiplexer_1 (
    .out0(demultiplexer_1_out0), .out1(demultiplexer_1_out1), .out2(demultiplexer_1_out2),
    .out3(demultiplexer_1_out3), .out4(demultiplexer_1_out4), .out5(demultiplexer_1_out5),
    .out6(demultiplexer_1_out6), .out7(demultiplexer_1_out7), .in(write), .sel(rd));
  Opdracht_4_3_4_4_main main_1 (.reset(reset), .D({12{1'b0}}), .write(demultiplexer_1_out0), .out_5(out_8), .C(C));
  Opdracht_4_3_4_4_main main_2 (.reset(reset), .D(data), .write(demultiplexer_1_out1), .out_5(out_9), .C(C));
  Opdracht_4_3_4_4_main main_3 (.reset(reset), .D(data), .write(demultiplexer_1_out2), .out_5(out_10), .C(C));
  Opdracht_4_3_4_4_main main_4 (.reset(reset), .D(data), .write(demultiplexer_1_out3), .out_5(out_11), .C(C));
  Opdracht_4_3_4_4_main main_5 (.reset(reset), .D(data), .write(demultiplexer_1_out4), .out_5(out_12), .C(C));
  Opdracht_4_3_4_4_main main_6 (.reset(reset), .D(data), .write(demultiplexer_1_out5), .out_5(out_13), .C(C));
  Opdracht_4_3_4_4_main main_7 (.reset(reset), .D(data), .write(demultiplexer_1_out6), .out_5(out_14), .C(C));
  Opdracht_4_3_4_4_main main_8 (.reset(reset), .D(data), .write(demultiplexer_1_out7), .out_5(out_15), .C(C));
  Multiplexer #(.select(3), .width(12), .enable("false")) multiplexer_1 (
    .in0(out_8), .in1(out_9), .in2(out_10), .in3(out_11), .in4(out_12), .in5(out_13), .in6(out_14),
    .in7(out_15), .out(S), .sel(rs));
  Multiplexer #(.select(3), .width(12), .enable("false")) multiplexer_2 (
    .in0(out_8), .in1(out_9), .in2(out_10), .in3(out_11), .in4(out_12), .in5(out_13), .in6(out_14),
    .in7(out_15), .out(T), .sel(rt));
endmodule

module Decoder (
  input  [15:0] in_1,
  output [2:0] operation,
  output [2:0] rd,
  output [2:0] rs,
  output [2:0] rt,
  output [3:0] funct
);


  assign funct = in_1[3:0];
  assign operation = in_1[15:13];
  assign rd = in_1[12:10];
  assign rs = in_1[9:7];
  assign rt = in_1[6:4];
endmodule

module Controller (
  input  [2:0] operation,
  input  [2:0] rd,
  input  [2:0] rs,
  input  [2:0] rt,
  input  [3:0] \function ,
  output [2:0] rd_2,
  output [2:0] rs_2,
  output [2:0] rt_2,
  output [3:0] funct,
  output sw,
  output lw,
  output [11:0] immediate,
  output lui,
  output jr,
  output brnz,
  output jal,
  output j,
  output exceptions
);

  wire addi, and_1_out, and_2_out, and_3_out, and_4_out, and_5_out, comparator_1_eq, comparator_2_eq,
       comparator_3_eq, comparator_4_eq, comparator_5_eq, comparator_6_eq, comparator_7_eq, comparator_8_eq,
       comparator_9_eq, comparator_10_eq, comparator_11_eq, comparator_12_eq, ldi, lui_t, not_1_out,
       not_2_out, not_3_out, not_4_out, not_5_out, not_6_out, not_7_out, not_8_out, or_1_out, subi;
  wire [3:0] multiplexer_1_out, n4_bit_adder_1_sum_0_1_2_3;
  wire [11:0] bit_extender_1_out, bit_extender_2_out, bit_extender_3_out, bit_extender_4_out,
       controlled_buffer_1_out, controlled_buffer_3_out;

  Multiplexer #(.width(4), .enable("false")) multiplexer_1 (
    .in0(4'b0000), .in1(4'b0001), .out(multiplexer_1_out), .sel(subi));
  _4_Bit_Adder u_4_bit_adder_1 (
    .Carry_in(1'b0), .A(\function ), .B(4'b1000), .SUM_0_1_2_3(n4_bit_adder_1_sum_0_1_2_3));  // open: P0, G0
  Comparator #(.width(3)) comparator_1 (.a(operation), .b(3'b111), .eq(comparator_1_eq));  // open: gt, lt
  Comparator #(.width(3)) comparator_2 (.a(operation), .b(3'b100), .eq(comparator_2_eq));  // open: gt, lt
  Comparator #(.width(3)) comparator_3 (.a(operation), .b(3'b011), .eq(comparator_3_eq));  // open: gt, lt
  Comparator #(.width(3)) comparator_4 (.a(operation), .b(3'b101), .eq(comparator_4_eq));  // open: gt, lt
  Comparator #(.width(3)) comparator_5 (.a(operation), .b(3'b110), .eq(comparator_5_eq));  // open: gt, lt
  Comparator #(.width(3)) comparator_6 (.a(operation), .b(3'b010), .eq(comparator_6_eq));  // open: gt, lt
  or or_1 (or_1_out, comparator_6_eq, comparator_7_eq);
  Comparator #(.width(3)) comparator_7 (.a(operation), .b(3'b001), .eq(comparator_7_eq));  // open: gt, lt
  Comparator #(.width(3)) comparator_8 (.a(operation), .b(3'b010), .eq(comparator_8_eq));  // open: gt, lt
  Comparator #(.width(3)) comparator_9 (.a(rt), .b(3'b000), .eq(comparator_9_eq));  // open: gt, lt
  not not_1 (not_1_out, comparator_9_eq);
  Comparator #(.width(3)) comparator_10 (.a(rs), .b(3'b000), .eq(comparator_10_eq));  // open: gt, lt
  not not_2 (not_2_out, comparator_10_eq);
  Comparator #(.width(3)) comparator_11 (.a(operation), .b(3'b000), .eq(comparator_11_eq));  // open: gt, lt
  not not_3 (not_3_out, comparator_12_eq);
  Comparator #(.width(4)) comparator_12 (.a(\function ), .b(4'b0000), .eq(comparator_12_eq));  // open: gt, lt
  and and_1 (and_1_out, or_1_out, \function [3]);
  and and_2 (and_2_out, comparator_8_eq, not_1_out);
  and and_3 (and_3_out, not_1_out, comparator_11_eq);
  and and_4 (and_4_out, not_2_out, comparator_11_eq);
  and and_5 (and_5_out, comparator_11_eq, not_3_out);
  Multiplexer #(.select(3), .width(3), .enable("false")) multiplexer_2 (
    .in0(rd), .in1(rd), .in2(rd), .in3(rd), .in4(rd), .in5(rd), .in6(3'b111), .in7(rd), .out(rd_2),
    .sel(operation));
  Multiplexer #(.select(3), .width(3), .enable("false")) multiplexer_3 (
    .in0(3'b000), .in1(rs), .in2(rs), .in3(3'b000), .in4(rd), .in5(rd), .in6(3'b111), .in7(rs), .out(rs_2),
    .sel(operation));
  Multiplexer #(.select(3), .width(3), .enable("false")) multiplexer_4 (
    .in0(3'b000), .in1(rt), .in2(3'b000), .in3(3'b000), .in4(3'b000), .in5(3'b000), .in6(3'b000), .in7(rd),
    .out(rt_2), .sel(operation));
  Multiplexer #(.select(3), .width(4), .enable("false")) multiplexer_5 (
    .in0(\function ), .in1(\function ), .in2(n4_bit_adder_1_sum_0_1_2_3), .in3(4'b0000),
    .in4(multiplexer_1_out), .in5(4'b0000), .in6(\function ), .in7(4'b0000), .out(funct), .sel(operation));
  and u_sw (sw, \function [0], comparator_1_eq);
  not not_4 (not_4_out, \function [0]);
  and u_lw (lw, not_4_out, comparator_1_eq);
  and u_subi (subi, \function [0], comparator_2_eq);
  not not_5 (not_5_out, \function [0]);
  and u_addi (addi, not_5_out, comparator_2_eq);
  and u_lui (lui_t, \function [0], comparator_3_eq);
  not not_6 (not_6_out, \function [0]);
  and u_ldi (ldi, not_6_out, comparator_3_eq);
  and u_jr (jr, \function [0], comparator_4_eq);
  not not_7 (not_7_out, \function [0]);
  and u_brnz (brnz, not_7_out, comparator_4_eq);
  and u_jal (jal, \function [0], comparator_5_eq);
  not not_8 (not_8_out, \function [0]);
  and u_j (j, not_8_out, comparator_5_eq);
  or or_2 (exceptions, and_1_out, and_2_out, and_3_out, and_4_out, and_5_out);
  or or_3 (lui, subi, addi, jr, lui_t, ldi);
  assign bit_extender_1_out = {{3{1'b0}}, {rs, rt, \function [3:1]}};  // Bit_Extender bit_extender_1
  assign bit_extender_2_out = {{3{rs[2]}}, {rs, rt, \function [3:1]}};  // Bit_Extender bit_extender_2
  assign controlled_buffer_1_out = brnz ? bit_extender_2_out : 12'bz;  // Controlled_Buffer controlled_buffer_1
  assign controlled_buffer_1_out = jr ? {3'b000, rs, rt, \function [3:1]} : 12'bz;  // Controlled_Buffer controlled_buffer_2
  assign controlled_buffer_3_out = ldi ? bit_extender_3_out : 12'bz;  // Controlled_Buffer controlled_buffer_3
  assign bit_extender_3_out = {{3{rs[2]}}, {rs, rt, \function [3:1]}};  // Bit_Extender bit_extender_3
  assign controlled_buffer_3_out = lui_t ? {rs, rt, \function [3:1], 3'b000} : 12'bz;  // Controlled_Buffer controlled_buffer_4
  assign bit_extender_4_out = {{6{1'b0}}, {rt, \function [3:1]}};  // Bit_Extender bit_extender_4
  Multiplexer #(.select(3), .width(12), .enable("false")) multiplexer_6 (
    .in3(controlled_buffer_3_out), .in4(bit_extender_1_out), .in5(controlled_buffer_1_out),
    .in6({rd, rs, rt, \function [3:1]}), .in7(bit_extender_4_out), .out(immediate), .sel(operation));  // open: in0, in1, in2

  // Other names for the same wires on the sheet: im[2:0] = \function [3:1]; MSB = \function [3]

  // Notes on the sheet:
  //   add
endmodule
