// Logisim project stan__Examen 15-16 eerste_zit again.circ as structural Verilog: 6 circuits, main circuit main
module main (
  output [10:0] out_1
);

  wire and_1_out, clock_out, comparator_1_lt, controller_1_alu_op, controller_1_branch_less_then,
       controller_1_jal, controller_1_jr, controller_1_peek, controller_1_regwrite,
       controller_1_setreturn_adress, controller_1_sp_decrease, controller_1_sp_increase,
       controller_1_stackread, controller_1_stackwrite, controller_1_useimm, or_1_out, or_2_out, reset_out;
  wire [1:0] decoder_1_op_code;
  wire [2:0] decoder_1_func, decoder_1_ri, decoder_1_ri_2, multiplexer_3_out;
  wire [7:0] adder_1_out, adder_2_out, alu_1_result, decoder_1_imm_adress, decoder_1_offset,
       multiplexer_1_out, multiplexer_2_out, multiplexer_4_out, multiplexer_5_out, multiplexer_6_out,
       multiplexer_7_out, multiplexer_8_out, pc_1_instruction_adress, ram_2_data, register_1_q,
       registers_1_ri, registers_1_rj, subtractor_1_out, subtractor_2_out;

  Multiplexer #(.width(8)) multiplexer_1 (
    .in0(multiplexer_2_out), .in1(decoder_1_offset), .out(multiplexer_1_out),
    .sel(controller_1_branch_less_then));  // open: en
  Multiplexer #(.width(8)) multiplexer_2 (
    .in0(decoder_1_imm_adress), .in1(adder_1_out), .out(multiplexer_2_out), .sel(controller_1_jr));  // open: en
  Button reset (.out(reset_out));
  Clock clock (.out(clock_out));
  PC pc_1 (
    .jump(or_1_out), .branch(and_1_out), .offset(multiplexer_1_out), .reset(reset_out), .clock(clock_out),
    .instruction_adress(pc_1_instruction_adress));
  decoder decoder_1 (
    .instructie(out_1), .OP_CODE(decoder_1_op_code), .Func(decoder_1_func), .Ri(decoder_1_ri),
    .Ri_2(decoder_1_ri_2), .imm_adress(decoder_1_imm_adress), .offset(decoder_1_offset));
  or or_1 (or_1_out, controller_1_jr, controller_1_jal);
  controller controller_1 (
    .OP_CODE(decoder_1_op_code), .FUNC_CODE(decoder_1_func), .jal(controller_1_jal), .jr(controller_1_jr),
    .branch_less_then(controller_1_branch_less_then), .StackRead(controller_1_stackread),
    .StackWrite(controller_1_stackwrite), .RegWrite(controller_1_regwrite), .UseImm(controller_1_useimm),
    .ALU_OP(controller_1_alu_op), .SetReturn_Adress(controller_1_setreturn_adress),
    .SP_Increase(controller_1_sp_increase), .SP_Decrease(controller_1_sp_decrease), .Peek(controller_1_peek));
  RAM #(.dataWidth(11)) ram_1 (.addr(pc_1_instruction_adress), .data(out_1));  // open: sel, clk, ld, clr
  Adder adder_1 (.a(registers_1_ri), .b(decoder_1_offset), .out(adder_1_out));  // open: cin, cout
  and and_1 (and_1_out, comparator_1_lt, controller_1_branch_less_then);
  or or_2 (or_2_out, controller_1_sp_decrease, controller_1_sp_increase);
  Multiplexer #(.width(3)) multiplexer_3 (
    .in0(decoder_1_ri), .in1(3'b111), .out(multiplexer_3_out), .sel(controller_1_setreturn_adress));  // open: en
  Multiplexer #(.width(8)) multiplexer_4 (
    .in0(multiplexer_6_out), .in1(decoder_1_imm_adress), .out(multiplexer_4_out), .sel(controller_1_useimm));  // open: en
  registers registers_1 (
    .write_register(controller_1_regwrite), .Write_Read_Ri(multiplexer_3_out), .Read_Rj(decoder_1_ri_2),
    .data(multiplexer_5_out), .reset(reset_out), .clock(clock_out), .Ri(registers_1_ri), .Rj(registers_1_rj));
  Multiplexer #(.width(8)) multiplexer_5 (
    .in0(multiplexer_4_out), .in1(pc_1_instruction_adress), .out(multiplexer_5_out),
    .sel(controller_1_setreturn_adress));  // open: en
  Multiplexer #(.width(8)) multiplexer_6 (
    .in0(alu_1_result), .in1(ram_2_data), .out(multiplexer_6_out), .sel(controller_1_peek));  // open: en
  Comparator comparator_1 (.a(registers_1_ri), .b(registers_1_rj), .lt(comparator_1_lt));  // open: gt, eq
  Multiplexer #(.width(8)) multiplexer_7 (
    .in0(adder_2_out), .in1(subtractor_1_out), .out(multiplexer_7_out), .sel(controller_1_sp_decrease));  // open: en
  ALU alu_1 (.A(registers_1_ri), .B(registers_1_rj), .ALU_CODE(controller_1_alu_op), .result(alu_1_result));
  Adder adder_2 (.a(register_1_q), .b(8'h1), .out(adder_2_out));  // open: cin, cout
  Subtractor subtractor_1 (.a(register_1_q), .b(8'h1), .out(subtractor_1_out));  // open: bin, bout
  Register register_1 (.D(multiplexer_7_out), .en(or_2_out), .Q(register_1_q), .clk(clock_out), .clr(reset_out));
  Subtractor subtractor_2 (.a(register_1_q), .b(8'h1), .out(subtractor_2_out));  // open: bin, bout
  Multiplexer #(.width(8)) multiplexer_8 (
    .in0(register_1_q), .in1(subtractor_2_out), .out(multiplexer_8_out), .sel(controller_1_peek));  // open: en
  RAM #(.bus("separate")) ram_2 (
    .addr(multiplexer_8_out), .din(registers_1_ri), .data(ram_2_data), .str(controller_1_stackwrite),
    .clk(clock_out), .ld(controller_1_stackread), .clr(reset_out));  // open: sel
endmodule

module PC (
  input  jump,
  input  branch,
  input  [7:0] offset,
  input  reset,
  input  clock,
  output [7:0] instruction_adress
);

  wire not_1_out, or_1_out;
  wire [7:0] adder_1_out, adder_2_out, multiplexer_1_out;

  Adder adder_1 (.a(offset), .b(adder_2_out), .out(adder_1_out));  // open: cin, cout
  or or_1 (or_1_out, jump, branch);
  Multiplexer #(.width(8)) multiplexer_1 (
    .in0(offset), .in1(adder_1_out), .out(multiplexer_1_out), .sel(branch));  // open: en
  Counter counter_1 (
    .load(or_1_out), .D(multiplexer_1_out), .count(not_1_out), .Q(instruction_adress), .clk(clock),
    .clr(reset));  // open: carry
  not not_1 (not_1_out, or_1_out);
  Adder adder_2 (.a(instruction_adress), .b(8'h1), .out(adder_2_out));  // open: cin, cout
endmodule

module registers (
  input  write_register,
  input  [2:0] Write_Read_Ri,
  input  [2:0] Read_Rj,
  input  [7:0] data,
  input  reset,
  input  clock,
  output [7:0] Ri,
  output [7:0] Rj
);

  wire demultiplexer_1_out0, demultiplexer_1_out1, demultiplexer_1_out2, demultiplexer_1_out3,
       demultiplexer_1_out4, demultiplexer_1_out5, demultiplexer_1_out6, demultiplexer_1_out7;
  wire [7:0] register_1_q, register_2_q, register_3_q, register_4_q, register_5_q, register_6_q,
       register_7_q, register_8_q;

  Demultiplexer #(.select(3)) demultiplexer_1 (
    .out0(demultiplexer_1_out0), .out1(demultiplexer_1_out1), .out2(demultiplexer_1_out2),
    .out3(demultiplexer_1_out3), .out4(demultiplexer_1_out4), .out5(demultiplexer_1_out5),
    .out6(demultiplexer_1_out6), .out7(demultiplexer_1_out7), .in(write_register), .sel(Write_Read_Ri));  // open: en
  Register register_1 (.en(demultiplexer_1_out0), .Q(register_1_q), .clk(clock), .clr(reset));  // open: D
  Register register_2 (.D(data), .en(demultiplexer_1_out1), .Q(register_2_q), .clk(clock), .clr(reset));
  Register register_3 (.D(data), .en(demultiplexer_1_out2), .Q(register_3_q), .clk(clock), .clr(reset));
  Register register_4 (.D(data), .en(demultiplexer_1_out3), .Q(register_4_q), .clk(clock), .clr(reset));
  Register register_5 (.D(data), .en(demultiplexer_1_out4), .Q(register_5_q), .clk(clock), .clr(reset));
  Register register_6 (.D(data), .en(demultiplexer_1_out5), .Q(register_6_q), .clk(clock), .clr(reset));
  Register register_7 (.D(data), .en(demultiplexer_1_out6), .Q(register_7_q), .clk(clock), .clr(reset));
  Register register_8 (.D(data), .en(demultiplexer_1_out7), .Q(register_8_q), .clk(clock), .clr(reset));
  Multiplexer #(.select(3), .width(8)) multiplexer_1 (
    .in0(register_1_q), .in1(register_2_q), .in2(register_3_q), .in3(register_4_q), .in4(register_5_q),
    .in5(register_6_q), .in6(register_7_q), .in7(register_8_q), .out(Ri), .sel(Write_Read_Ri));  // open: en
  Multiplexer #(.select(3), .width(8)) multiplexer_2 (
    .in0(register_1_q), .in1(register_2_q), .in2(register_3_q), .in3(register_4_q), .in4(register_5_q),
    .in5(register_6_q), .in6(register_7_q), .in7(register_8_q), .out(Rj), .sel(Read_Rj));  // open: en
endmodule

module ALU (
  input  ALU_CODE,
  input  [7:0] A,
  input  [7:0] B,
  output [7:0] result
);

  wire [7:0] adder_1_out, subtractor_1_out;

  Adder adder_1 (.a(A), .b(B), .out(adder_1_out));  // open: cin, cout
  Subtractor subtractor_1 (.a(A), .b(B), .out(subtractor_1_out));  // open: bin, bout
  Multiplexer #(.width(8)) multiplexer_1 (
    .in0(subtractor_1_out), .in1(adder_1_out), .out(result), .sel(ALU_CODE));  // open: en
endmodule

module decoder (
  input  [10:0] instructie,
  output [1:0] OP_CODE,
  output [2:0] Func,
  output [2:0] Ri,
  output [2:0] Ri_2,
  output [7:0] imm_adress,
  output [7:0] offset
);

  wire and_1_out;

  and and_1 (and_1_out, instructie[9], instructie[10]);
  Multiplexer #(.width(8)) multiplexer_1 (
    .in0({{3{instructie[5]}}, instructie[4:0]}), .in1(instructie[8:1]), .out(imm_adress), .sel(and_1_out));  // open: en
  Multiplexer #(.width(8)) multiplexer_2 (
    .in0({{6{instructie[2]}}, instructie[1:0]}), .in1({{4{instructie[5]}}, instructie[4:1]}), .out(offset),
    .sel(and_1_out));  // open: en

  assign Func = instructie[2:0];
  assign OP_CODE = instructie[10:9];
  assign Ri = instructie[8:6];
  assign Ri_2 = instructie[5:3];
endmodule

module controller (
  input  [1:0] OP_CODE,
  input  [2:0] FUNC_CODE,
  output jal,
  output jr,
  output branch_less_then,
  output StackRead,
  output StackWrite,
  output RegWrite,
  output UseImm,
  output ALU_OP,
  output SetReturn_Adress,
  output SP_Increase,
  output SP_Decrease,
  output Peek
);

  wire and_1_out, and_2_out, and_4_out, and_5_out, and_6_out, and_7_out, and_8_out, and_9_out, and_10_out,
       and_11_out, and_13_out, or_1_out, or_2_out;

  and and_1 (and_1_out, OP_CODE[0], OP_CODE[1]);
  and and_2 (and_2_out, ~OP_CODE[1], ~OP_CODE[0]);  // AND_Gate
  and and_3 (UseImm, OP_CODE[1], ~OP_CODE[0]);  // AND_Gate
  and and_4 (and_4_out, FUNC_CODE[0], FUNC_CODE[1], ~FUNC_CODE[2]);  // AND_Gate
  and and_5 (and_5_out, ~FUNC_CODE[0], ~FUNC_CODE[1], FUNC_CODE[2]);  // AND_Gate
  and and_6 (and_6_out, ~FUNC_CODE[2], ~FUNC_CODE[1], ~FUNC_CODE[0]);  // AND_Gate
  and and_7 (and_7_out, ~FUNC_CODE[2], ~FUNC_CODE[1], FUNC_CODE[0]);  // AND_Gate
  and and_8 (and_8_out, ~FUNC_CODE[2], FUNC_CODE[1], FUNC_CODE[0]);  // AND_Gate
  and and_9 (and_9_out, FUNC_CODE[2], ~FUNC_CODE[1], ~FUNC_CODE[0]);  // AND_Gate
  or or_1 (or_1_out, and_4_out, and_5_out);
  and and_10 (and_10_out, ~FUNC_CODE[2], FUNC_CODE[1], ~FUNC_CODE[0]);  // AND_Gate
  and and_11 (and_11_out, and_2_out, or_2_out);
  or or_2 (or_2_out, and_6_out, and_7_out, and_8_out, and_9_out);
  and and_12 (SP_Decrease, and_8_out, and_2_out);
  and and_13 (and_13_out, and_9_out, and_2_out);
  and and_14 (jal, and_1_out, ~FUNC_CODE[0]);  // AND_Gate
  and and_15 (jr, and_1_out, FUNC_CODE[0]);
  and and_16 (branch_less_then, ~OP_CODE[1], OP_CODE[0]);  // AND_Gate
  and and_17 (StackRead, and_2_out, or_1_out);
  and and_18 (SP_Increase, and_2_out, and_10_out);
  or or_3 (RegWrite, and_11_out, jal, UseImm);
  or or_4 (Peek, SP_Decrease, and_13_out);

  assign ALU_OP = FUNC_CODE[0];
  assign SetReturn_Adress = jal;
  assign StackWrite = SP_Increase;
endmodule
