// Logisim project torben_examen_1.circ as structural Verilog: 5 circuits, main circuit main
module main (
  input  Reset
);

  wire and_1_out, Clock_out, comparator_1_eq, control_unit_1_branch_absolute, control_unit_1_brnch_relative,
       control_unit_1_use_immediate, not_1_out;
  wire [1:0] control_unit_1_opcode;
  wire [3:0] control_unit_1_rd, control_unit_1_rs, control_unit_1_rt;
  wire [7:0] alu_1_r, control_unit_1_immediate, multiplexer_1_out, program_counter_1_instruction_address,
       register_file_1_s, register_file_1_t;
  wire [11:0] rom_1_data;

  program_counter program_counter_1 (
    .clock(Clock_out), .reset(Reset), .instruction_address(program_counter_1_instruction_address),
    .absolute(control_unit_1_branch_absolute), .relative(and_1_out), .address(control_unit_1_immediate));
  Clock Clock (.out(Clock_out));
  and and_1 (and_1_out, not_1_out, control_unit_1_brnch_relative);
  control_unit control_unit_1 (
    .Instruction(rom_1_data), .rd(control_unit_1_rd), .rt(control_unit_1_rt), .rs(control_unit_1_rs),
    .immediate(control_unit_1_immediate), .opcode(control_unit_1_opcode),
    .use_immediate(control_unit_1_use_immediate), .branch_absolute(control_unit_1_branch_absolute),
    .brnch_relative(control_unit_1_brnch_relative));
  ROM #(.dataWidth(12)) rom_1 (.addr(program_counter_1_instruction_address), .data(rom_1_data));  // open: sel
  register_file register_file_1 (
    .rs(control_unit_1_rs), .data(alu_1_r), .clock(Clock_out), .reset(Reset), .rt(control_unit_1_rt),
    .S(register_file_1_s), .T(register_file_1_t), .rd(control_unit_1_rd));
  Comparator comparator_1 (.a({8{1'b0}}), .b(register_file_1_s), .eq(comparator_1_eq));  // open: gt, lt
  not not_1 (not_1_out, comparator_1_eq);
  Multiplexer #(.width(8)) multiplexer_1 (
    .in0(register_file_1_s), .in1(control_unit_1_immediate), .out(multiplexer_1_out),
    .sel(control_unit_1_use_immediate));  // open: en
  ALU alu_1 (.A(multiplexer_1_out), .B(register_file_1_t), .R(alu_1_r), .Opcode(control_unit_1_opcode));

  // Notes on the sheet:
  //   contents of rom_1 (hex, n*v repeats v):
  //   401 9fe
endmodule

// pc
module program_counter (
  input  absolute,
  input  relative,
  input  [7:0] address,
  input  clock,
  input  reset,
  output [7:0] instruction_address
);

  wire [7:0] adder_1_out, multiplexer_1_out, multiplexer_2_out;

  Multiplexer #(.width(8)) multiplexer_1 (
    .in0(adder_1_out), .in1(address), .out(multiplexer_1_out), .sel(absolute));  // open: en
  Register register_1 (.D(multiplexer_1_out), .Q(instruction_address), .clk(clock), .clr(reset));  // open: en
  Multiplexer #(.width(8)) multiplexer_2 (
    .in0(8'h1), .in1(address), .out(multiplexer_2_out), .sel(relative));  // open: en
  Adder adder_1 (.a(multiplexer_2_out), .b(instruction_address), .out(adder_1_out), .cin(relative));  // open: cout
endmodule

module ALU (
  input  [1:0] Opcode,
  input  [7:0] A,
  input  [7:0] B,
  output [7:0] R
);

  wire [7:0] adder_1_out, and_1_out, subtractor_1_out;

  assign and_1_out = A & B;  // AND_Gate and_1, 8 bits wide
  Adder adder_1 (.a(A), .b(B), .out(adder_1_out));  // open: cin, cout
  Subtractor subtractor_1 (.a(A), .b(B), .out(subtractor_1_out));  // open: bin, bout
  Multiplexer #(.select(2), .width(8)) multiplexer_1 (
    .in0(A), .in1(and_1_out), .in2(adder_1_out), .in3(subtractor_1_out), .out(R), .sel(Opcode));  // open: en
endmodule

// RegFile
module register_file (
  input  [3:0] rs,
  input  [3:0] rt,
  input  [7:0] data,
  input  clock,
  input  reset,
  input  [3:0] rd,
  output [7:0] S,
  output [7:0] T
);

  wire demultiplexer_1_out1, demultiplexer_1_out2, demultiplexer_1_out3, demultiplexer_1_out4,
       demultiplexer_1_out5, demultiplexer_1_out6, demultiplexer_1_out7, demultiplexer_1_out8,
       demultiplexer_1_out9, demultiplexer_1_out10, demultiplexer_1_out11, demultiplexer_1_out12,
       demultiplexer_1_out13, demultiplexer_1_out14, demultiplexer_1_out15;
  wire [7:0] register_1_q, register_2_q, register_3_q, register_4_q, register_5_q, register_6_q,
       register_7_q, register_8_q, register_9_q, register_10_q, register_11_q, register_12_q, register_13_q,
       register_14_q, register_15_q, register_16_q;

  Demultiplexer #(.select(4)) demultiplexer_1 (
    .out1(demultiplexer_1_out1), .out2(demultiplexer_1_out2), .out3(demultiplexer_1_out3),
    .out4(demultiplexer_1_out4), .out5(demultiplexer_1_out5), .out6(demultiplexer_1_out6),
    .out7(demultiplexer_1_out7), .out8(demultiplexer_1_out8), .out9(demultiplexer_1_out9),
    .out10(demultiplexer_1_out10), .out11(demultiplexer_1_out11), .out12(demultiplexer_1_out12),
    .out13(demultiplexer_1_out13), .out14(demultiplexer_1_out14), .out15(demultiplexer_1_out15), .in(1'b1),
    .sel(rd));  // open: out0, en
  Multiplexer #(.select(4), .width(8)) multiplexer_1 (
    .in0(register_1_q), .in1(register_3_q), .in2(register_2_q), .in3(register_4_q), .in4(register_5_q),
    .in5(register_6_q), .in6(register_7_q), .in7(register_8_q), .in8(register_9_q), .in9(register_11_q),
    .in10(register_10_q), .in11(register_12_q), .in12(register_13_q), .in13(register_14_q),
    .in14(register_15_q), .in15(register_16_q), .out(S), .sel(rs));  // open: en
  Register register_1 (.Q(register_1_q), .clk(clock), .clr(reset));  // open: D, en
  Register register_2 (.D(data), .en(demultiplexer_1_out2), .Q(register_2_q), .clk(clock), .clr(reset));
  Register register_3 (.D(data), .en(demultiplexer_1_out1), .Q(register_3_q), .clk(clock), .clr(reset));
  Register register_4 (.D(data), .en(demultiplexer_1_out3), .Q(register_4_q), .clk(clock), .clr(reset));
  Multiplexer #(.select(4), .width(8)) multiplexer_2 (
    .in0(register_1_q), .in1(register_3_q), .in2(register_2_q), .in3(register_4_q), .in4(register_5_q),
    .in5(register_6_q), .in6(register_7_q), .in7(register_8_q), .in8(register_9_q), .in9(register_11_q),
    .in10(register_10_q), .in11(register_12_q), .in12(register_13_q), .in13(register_14_q),
    .in14(register_15_q), .in15(register_16_q), .out(T), .sel(rt));  // open: en
  Register register_5 (.D(data), .en(demultiplexer_1_out4), .Q(register_5_q), .clk(clock), .clr(reset));
  Register register_6 (.D(data), .en(demultiplexer_1_out5), .Q(register_6_q), .clk(clock), .clr(reset));
  Register register_7 (.D(data), .en(demultiplexer_1_out6), .Q(register_7_q), .clk(clock), .clr(reset));
  Register register_8 (.D(data), .en(demultiplexer_1_out7), .Q(register_8_q), .clk(clock), .clr(reset));
  Register register_9 (.D(data), .en(demultiplexer_1_out8), .Q(register_9_q), .clk(clock), .clr(reset));
  Register register_10 (.D(data), .en(demultiplexer_1_out10), .Q(register_10_q), .clk(clock), .clr(reset));
  Register register_11 (.D(data), .en(demultiplexer_1_out9), .Q(register_11_q), .clk(clock), .clr(reset));
  Register register_12 (.D(data), .en(demultiplexer_1_out11), .Q(register_12_q), .clk(clock), .clr(reset));
  Register register_13 (.D(data), .en(demultiplexer_1_out12), .Q(register_13_q), .clk(clock), .clr(reset));
  Register register_14 (.D(data), .en(demultiplexer_1_out13), .Q(register_14_q), .clk(clock), .clr(reset));
  Register register_15 (.D(data), .en(demultiplexer_1_out14), .Q(register_15_q), .clk(clock), .clr(reset));
  Register register_16 (.D(data), .en(demultiplexer_1_out15), .Q(register_16_q), .clk(clock), .clr(reset));
endmodule

// Control
module control_unit (
  input  [11:0] Instruction,
  output [3:0] rd,
  output [3:0] rt,
  output [3:0] rs,
  output [7:0] immediate,
  output use_immediate,
  output [1:0] opcode,
  output brnch_relative,
  output branch_absolute
);

  wire or_1_out;
  wire [3:2] and_1_out;

  Comparator #(.width(4), .mode("unsigned")) comparator_1 (
    .a(Instruction[11:8]), .b(4'b0011), .gt(use_immediate));  // open: eq, lt
  assign {and_1_out, opcode} = Instruction[11:8] & 4'b0011;  // AND_Gate and_1, 4 bits wide
  Comparator #(.width(4), .mode("unsigned")) comparator_2 (
    .a(Instruction[11:8]), .b(4'b1001), .eq(brnch_relative));  // open: gt, lt
  Comparator #(.width(4), .mode("unsigned")) comparator_3 (
    .a(Instruction[11:8]), .b(4'b1000), .eq(branch_absolute));  // open: gt, lt
  or or_1 (or_1_out, Instruction[8], Instruction[9], Instruction[10], Instruction[11]);
  Multiplexer #(.width(4)) multiplexer_1 (.in0(Instruction[7:4]), .in1(4'b1111), .out(rd), .sel(or_1_out));  // open: en
  Multiplexer #(.width(4)) multiplexer_2 (
    .in0(Instruction[3:0]), .in1(4'b1111), .out(rs), .sel(use_immediate));  // open: en

  assign immediate = Instruction[7:0];
  assign rt = Instruction[7:4];
endmodule
