// Logisim project torben_examen_2.circ as structural Verilog: 5 circuits, main circuit main
module main (
  input  Reset
);

  wire and_1_out, Clock_out, comparator_1_gt, control_unit_1_br_absoluet, control_unit_1_br_relative,
       control_unit_1_constant, control_unit_1_jal, control_unit_1_memread, control_unit_1_memwrite,
       control_unit_1_reginput, control_unit_1_regwrite, or_1_out, or_2_out;
  wire [1:0] control_unit_1_alu_op;
  wire [2:0] control_unit_1_rd, control_unit_1_rs, control_unit_1_rt;
  wire [7:0] alu_1_r, control_unit_1_br_value, multiplexer_1_out, multiplexer_2_out, multiplexer_3_out,
       multiplexer_4_out, program_counter_1_instruction_address, ram_1_data, register_file_1_address_pointer,
       register_file_1_s, register_file_1_t;
  wire [8:0] rom_1_data;

  program_counter program_counter_1 (
    .Branch_Offset(control_unit_1_br_value), .Branch_Relative(and_1_out),
    .Branch_Absolute(control_unit_1_br_absoluet),
    .Instruction_Address(program_counter_1_instruction_address), .Clock(Clock_out), .Reset(Reset));
  Clock Clock (.out(Clock_out));
  control_unit control_unit_1 (
    .Instruction(rom_1_data), .regwrite(control_unit_1_regwrite), .rs(control_unit_1_rs),
    .rd(control_unit_1_rd), .rt(control_unit_1_rt), .ALU_op(control_unit_1_alu_op),
    .Constant(control_unit_1_constant), .RegInput(control_unit_1_reginput),
    .memwrite(control_unit_1_memwrite), .memread(control_unit_1_memread),
    .br_relative(control_unit_1_br_relative), .br_absoluet(control_unit_1_br_absoluet),
    .br_value(control_unit_1_br_value), .jal(control_unit_1_jal));
  ROM #(.dataWidth(9)) rom_1 (.addr(program_counter_1_instruction_address), .data(rom_1_data));  // open: sel
  and and_1 (and_1_out, comparator_1_gt, control_unit_1_br_relative);
  register_file register_file_1 (
    .rs(control_unit_1_rs), .Data(multiplexer_2_out), .Clock(Clock_out), .Reset(Reset),
    .Write(control_unit_1_regwrite), .rt(control_unit_1_rt),
    .Address_Pointer(register_file_1_address_pointer), .rd(control_unit_1_rd), .S(register_file_1_s),
    .T(register_file_1_t));
  Multiplexer #(.width(8)) multiplexer_1 (
    .in0(register_file_1_t), .in1(8'h1), .out(multiplexer_1_out), .sel(control_unit_1_constant));  // open: en
  Multiplexer #(.width(8)) multiplexer_2 (
    .in0(alu_1_r), .in1(multiplexer_3_out), .out(multiplexer_2_out), .sel(control_unit_1_reginput));  // open: en
  alu alu_1 (.A(register_file_1_s), .B(multiplexer_1_out), .R(alu_1_r), .Operation_Code(control_unit_1_alu_op));
  Multiplexer #(.width(8)) multiplexer_3 (
    .in0({8{1'b0}}), .in1(ram_1_data), .out(multiplexer_3_out), .sel(control_unit_1_memread));  // open: en
  Multiplexer #(.width(8)) multiplexer_4 (
    .in0(multiplexer_2_out), .in1(program_counter_1_instruction_address), .out(multiplexer_4_out),
    .sel(control_unit_1_jal));  // open: en
  or or_1 (or_1_out, control_unit_1_br_relative, control_unit_1_memread);
  or or_2 (or_2_out, control_unit_1_memwrite, control_unit_1_jal);
  RAM #(.bus("separate")) ram_1 (
    .addr(register_file_1_address_pointer), .din(multiplexer_4_out), .data(ram_1_data), .str(or_2_out),
    .clk(Clock_out), .ld(or_1_out), .clr(Reset));  // open: sel
  Comparator comparator_1 (.a(ram_1_data), .b({8{1'b0}}), .gt(comparator_1_gt));  // open: eq, lt

  // Notes on the sheet:
  //   Instruction memory
  //   contents of rom_1 (hex, n*v repeats v):
  //   5 9 39 d 39 14a 14 3a c 39 84
  //   Memory
endmodule

// PC
module program_counter (
  input  Clock,
  input  Reset,
  input  [7:0] Branch_Offset,
  input  Branch_Relative,
  input  Branch_Absolute,
  output [7:0] Instruction_Address
);

  wire [7:0] adder_1_out, multiplexer_1_out, multiplexer_2_out;

  Register #(.trigger("falling")) register_1 (
    .D(multiplexer_2_out), .en(1'b1), .Q(Instruction_Address), .clk(Clock), .clr(Reset));
  Multiplexer #(.width(8)) multiplexer_1 (
    .in0(8'h1), .in1(Branch_Offset), .out(multiplexer_1_out), .sel(Branch_Relative));  // open: en
  Adder adder_1 (
    .a(multiplexer_1_out), .b(Instruction_Address), .out(adder_1_out), .cin(Branch_Relative));  // open: cout
  Multiplexer #(.width(8)) multiplexer_2 (
    .in0(adder_1_out), .in1(Branch_Offset), .out(multiplexer_2_out), .sel(Branch_Absolute));  // open: en
endmodule

// ALU
module alu (
  input  [1:0] Operation_Code,
  input  [7:0] A,
  input  [7:0] B,
  output [7:0] R
);

  wire [7:0] adder_1_out, not_1_out, or_1_out, subtractor_1_out;

  assign or_1_out = A | B;  // OR_Gate or_1, 8 bits wide
  assign not_1_out = ~A;  // NOT_Gate not_1, 8 bits wide
  Adder adder_1 (.a(A), .b(B), .out(adder_1_out));  // open: cin, cout
  Subtractor subtractor_1 (.a(A), .b(B), .out(subtractor_1_out));  // open: bin, bout
  Multiplexer #(.select(2), .width(8)) multiplexer_1 (
    .in0(or_1_out), .in1(adder_1_out), .in2(subtractor_1_out), .in3(not_1_out), .out(R), .sel(Operation_Code));  // open: en
endmodule

// Reg file
module register_file (
  input  [2:0] rs,
  input  [2:0] rt,
  input  [7:0] Data,
  input  Clock,
  input  Reset,
  input  [2:0] rd,
  input  Write,
  output [7:0] S,
  output [7:0] T,
  output [7:0] Address_Pointer
);

  wire demultiplexer_1_out1, demultiplexer_1_out2, demultiplexer_1_out3, demultiplexer_1_out4,
       demultiplexer_1_out5, demultiplexer_1_out6, demultiplexer_1_out7;
  wire [7:0] r0_q, r1_q, r2_q, r3_q, r4_q, r5_q, r6_q;

  Demultiplexer #(.select(3)) demultiplexer_1 (
    .out1(demultiplexer_1_out1), .out2(demultiplexer_1_out2), .out3(demultiplexer_1_out3),
    .out4(demultiplexer_1_out4), .out5(demultiplexer_1_out5), .out6(demultiplexer_1_out6),
    .out7(demultiplexer_1_out7), .in(Write), .sel(rd));  // open: out0, en
  Register #(.trigger("falling")) r0 (.Q(r0_q));  // open: D, en, clk, clr
  Multiplexer #(.select(3), .width(8)) multiplexer_1 (
    .in0(r0_q), .in1(r1_q), .in2(r2_q), .in3(r3_q), .in4(r4_q), .in5(r5_q), .in6(r6_q),
    .in7(Address_Pointer), .out(S), .sel(rs));  // open: en
  Register #(.trigger("falling")) r1 (.D(Data), .en(demultiplexer_1_out1), .Q(r1_q), .clk(Clock), .clr(Reset));
  Multiplexer #(.select(3), .width(8)) multiplexer_2 (
    .in0(r0_q), .in1(r1_q), .in2(r2_q), .in3(r3_q), .in4(r4_q), .in5(r5_q), .in6(r6_q),
    .in7(Address_Pointer), .out(T), .sel(rt));  // open: en
  Register #(.trigger("falling")) r2 (.D(Data), .en(demultiplexer_1_out2), .Q(r2_q), .clk(Clock), .clr(Reset));
  Register #(.trigger("falling")) r3 (.D(Data), .en(demultiplexer_1_out3), .Q(r3_q), .clk(Clock), .clr(Reset));
  Register #(.trigger("falling")) r5 (.D(Data), .en(demultiplexer_1_out5), .Q(r5_q), .clk(Clock), .clr(Reset));
  Register #(.trigger("falling")) r4 (.D(Data), .en(demultiplexer_1_out4), .Q(r4_q), .clk(Clock), .clr(Reset));
  Register #(.trigger("falling")) r6 (.D(Data), .en(demultiplexer_1_out6), .Q(r6_q), .clk(Clock), .clr(Reset));
  Register #(.trigger("falling")) r7 (
    .D(Data), .en(demultiplexer_1_out7), .Q(Address_Pointer), .clk(Clock), .clr(Reset));
endmodule

// Control unit
module control_unit (
  input  [8:0] Instruction,
  output [7:0] br_value,
  output br_relative,
  output br_absoluet,
  output memread,
  output jal,
  output memwrite,
  output regwrite,
  output Constant,
  output RegInput,
  output [2:0] rs,
  output [2:0] rd,
  output [2:0] rt,
  output [1:0] ALU_op
);

  wire and_1_out, and_3_out, comparator_1_gt, comparator_2_eq, comparator_3_gt, comparator_3_lt,
       comparator_4_eq, comparator_4_lt, comparator_5_eq, comparator_6_eq, xor_1_out;
  wire [2:0] or_1_out, xor_2_out;
  wire [2:2] multiplexer_1_out;

  assign br_value = {{2{1'b0}}, Instruction[5:0]};  // Bit_Extender bit_extender_1
  Comparator #(.width(3), .mode("unsigned")) comparator_1 (
    .a(Instruction[8:6]), .b(3'b001), .gt(comparator_1_gt), .eq(br_relative));  // open: lt
  Comparator #(.width(3), .mode("unsigned")) comparator_2 (
    .a(Instruction[2:0]), .b(3'b100), .eq(comparator_2_eq));  // open: gt, lt
  Comparator #(.width(3), .mode("unsigned")) comparator_3 (
    .a(3'b011), .b(Instruction[8:6]), .gt(comparator_3_gt), .eq(jal), .lt(comparator_3_lt));
  Comparator #(.width(3), .mode("unsigned")) comparator_4 (
    .a(Instruction[2:0]), .b(3'b101), .eq(comparator_4_eq), .lt(comparator_4_lt));  // open: gt
  Comparator #(.width(3), .mode("unsigned")) comparator_5 (
    .a(Instruction[8:6]), .b(3'b000), .eq(comparator_5_eq));  // open: gt, lt
  ExactlyOne xor_1 (.out(xor_1_out), .in0(Instruction[0]), .in1(Instruction[1]), .in2(Instruction[2]));
  Comparator #(.width(3), .mode("unsigned")) comparator_6 (
    .a(3'b000), .b(or_1_out), .eq(comparator_6_eq));  // open: gt, lt
  assign or_1_out = Instruction[8:6] | Instruction[2:0];  // OR_Gate or_1, 3 bits wide
  Multiplexer #(.width(3)) multiplexer_1 (
    .in0(Instruction[2:0]), .in1(xor_2_out), .out({multiplexer_1_out[2], ALU_op}), .sel(Instruction[8]));  // open: en
  assign xor_2_out = Instruction[8:6] ^ 3'b100;  // XOR_Gate xor_2, 3 bits wide
  and and_1 (and_1_out, comparator_1_gt, comparator_3_gt);
  or or_2 (br_absoluet, and_1_out, jal);
  and and_2 (memread, comparator_2_eq, comparator_5_eq);
  and and_3 (and_3_out, comparator_5_eq, comparator_4_eq);
  and and_4 (regwrite, comparator_4_lt, comparator_5_eq);
  and and_5 (Constant, comparator_5_eq, xor_1_out);
  or or_3 (memwrite, comparator_3_lt, and_3_out);
  or or_4 (RegInput, memread, comparator_6_eq);

  assign rd = Instruction[5:3];
  assign rs = Instruction[5:3];
  assign rt = Instruction[2:0];
endmodule
