// Logisim project torben_examen_3.circ as structural Verilog: 6 circuits, main circuit main
module main (
);

  wire and_1_out, and_2_out, clock_out, comparator_1_eq, control_unit_1_branch, control_unit_1_jump,
       control_unit_1_reg_write, control_unit_1_sp_decrease, control_unit_1_sp_increase,
       control_unit_1_stack_peak, control_unit_1_stack_push, control_unit_1_use_immediate, or_1_out,
       or_2_out, reset_out, xnor_1_out;
  wire [1:0] control_unit_1_alu_op, decoder_1_function, decoder_1_op_code, decoder_1_ri, decoder_1_rj;
  wire [7:0] adder_1_out, adder_2_out, alu_1_r, decoder_1_immediate, multiplexer_1_out, multiplexer_2_out,
       multiplexer_3_out, multiplexer_4_out, multiplexer_5_out, multiplexer_6_out, multiplexer_7_out,
       program_counter_1_instruciton_address, ram_1_data, register_file_1_ri_2, register_file_1_rj_2,
       Stack_Pointer_q, subtractor_1_out;
  wire [11:0] rom_1_data;

  program_counter program_counter_1 (
    .address(multiplexer_1_out), .clock(clock_out), .reset(reset_out),
    .instruciton_address(program_counter_1_instruciton_address), .jump(control_unit_1_jump),
    .branch(and_2_out));
  Clock clock (.out(clock_out));
  Button reset (.out(reset_out));
  Multiplexer #(.width(8)) multiplexer_1 (
    .in0(adder_1_out), .in1(multiplexer_2_out), .out(multiplexer_1_out), .sel(control_unit_1_jump));  // open: en
  and and_1 (and_1_out, control_unit_1_stack_peak, control_unit_1_jump);
  Multiplexer #(.width(8)) multiplexer_2 (
    .in0(decoder_1_immediate), .in1(ram_1_data), .out(multiplexer_2_out), .sel(and_1_out));  // open: en
  ROM #(.dataWidth(12)) rom_1 (.addr(program_counter_1_instruciton_address), .data(rom_1_data));  // open: sel
  decoder decoder_1 (
    .instruction(rom_1_data), .op_code(decoder_1_op_code), .\function (decoder_1_function),
    .rj(decoder_1_rj), .ri(decoder_1_ri), .immediate(decoder_1_immediate));
  register_file register_file_1 (
    .ri(decoder_1_ri), .\input (ram_1_data), .clock(clock_out), .reset(reset_out),
    .write(control_unit_1_reg_write), .rj(decoder_1_rj), .ri_2(register_file_1_ri_2),
    .rj_2(register_file_1_rj_2));
  xnor xnor_1 (xnor_1_out, ~comparator_1_eq, control_unit_1_stack_peak);  // XNOR_Gate
  and and_2 (and_2_out, xnor_1_out, control_unit_1_branch);
  control_unit control_unit_1 (
    .alu_op(control_unit_1_alu_op), .branch(control_unit_1_branch), .jump(control_unit_1_jump),
    .stack_push(control_unit_1_stack_push), .stack_peak(control_unit_1_stack_peak),
    .reg_write(control_unit_1_reg_write), .use_immediate(control_unit_1_use_immediate),
    .sp_decrease(control_unit_1_sp_decrease), .sp_increase(control_unit_1_sp_increase),
    .op_code(decoder_1_function), .fnction(decoder_1_op_code));
  Multiplexer #(.width(8)) multiplexer_3 (
    .in0(register_file_1_ri_2), .in1(ram_1_data), .out(multiplexer_3_out), .sel(control_unit_1_use_immediate));  // open: en
  Multiplexer #(.width(8)) multiplexer_4 (
    .in0(register_file_1_rj_2), .in1(decoder_1_immediate), .out(multiplexer_4_out),
    .sel(control_unit_1_use_immediate));  // open: en
  Adder adder_1 (.a(decoder_1_immediate), .b(8'h1), .out(adder_1_out));  // open: cin, cout
  ALU alu_1 (.A(multiplexer_3_out), .B(multiplexer_4_out), .R(alu_1_r), .op(control_unit_1_alu_op));
  or or_1 (or_1_out, control_unit_1_sp_decrease, control_unit_1_sp_increase);
  Multiplexer #(.width(8)) multiplexer_5 (
    .in0(alu_1_r), .in1(register_file_1_ri_2), .out(multiplexer_5_out), .sel(control_unit_1_stack_push));  // open: en
  Register Stack_Pointer (.D(adder_2_out), .en(or_1_out), .Q(Stack_Pointer_q), .clk(clock_out), .clr(reset_out));
  Multiplexer #(.width(8)) multiplexer_6 (
    .in0(8'h1), .in1({8{1'b1}}), .out(multiplexer_6_out), .sel(control_unit_1_sp_decrease));  // open: en
  Adder adder_2 (.a(Stack_Pointer_q), .b(multiplexer_6_out), .out(adder_2_out));  // open: cin, cout
  Subtractor subtractor_1 (.a(Stack_Pointer_q), .b(8'h1), .out(subtractor_1_out));  // open: bin, bout
  or or_2 (or_2_out, control_unit_1_sp_decrease, control_unit_1_stack_peak);
  Multiplexer #(.width(8)) multiplexer_7 (
    .in0(Stack_Pointer_q), .in1(subtractor_1_out), .out(multiplexer_7_out), .sel(or_2_out));  // open: en
  RAM #(.bus("separate")) ram_1 (
    .addr(multiplexer_7_out), .din(multiplexer_5_out), .data(ram_1_data), .str(control_unit_1_sp_increase),
    .clk(clock_out), .clr(reset_out));  // open: sel, ld
  Comparator comparator_1 (.a({8{1'b0}}), .b(ram_1_data), .eq(comparator_1_eq));  // open: gt, lt

  // Notes on the sheet:
  //   Instruction Memory
  //   contents of rom_1 (hex, n*v repeats v):
  //   800 401 980 260 980 a00 960 880 e03
  //   Data Memory (Stack)
endmodule

module ALU (
  input  [1:0] op,
  input  [7:0] A,
  input  [7:0] B,
  output [7:0] R
);

  wire [7:0] adder_1_out, and_1_out, or_1_out, subtractor_1_out;

  assign or_1_out = A | B;  // OR_Gate or_1, 8 bits wide
  assign and_1_out = A & B;  // AND_Gate and_1, 8 bits wide
  Adder adder_1 (.a(A), .b(B), .out(adder_1_out));  // open: cin, cout
  Subtractor subtractor_1 (.a(A), .b(B), .out(subtractor_1_out));  // open: bin, bout
  Multiplexer #(.select(2), .width(8)) multiplexer_1 (
    .in0(or_1_out), .in1(and_1_out), .in2(adder_1_out), .in3(subtractor_1_out), .out(R), .sel(op));  // open: en
endmodule

// PC
module program_counter (
  input  jump,
  input  branch,
  input  [7:0] address,
  input  clock,
  input  reset,
  output [7:0] instruciton_address
);

  wire [7:0] adder_1_out, multiplexer_1_out, multiplexer_2_out;

  Multiplexer #(.width(8)) multiplexer_1 (
    .in0(adder_1_out), .in1(address), .out(multiplexer_1_out), .sel(jump));  // open: en
  Multiplexer #(.width(8)) multiplexer_2 (
    .in0(8'h1), .in1(address), .out(multiplexer_2_out), .sel(branch));  // open: en
  Register register_1 (.D(multiplexer_1_out), .Q(instruciton_address), .clk(clock), .clr(reset));  // open: en
  Adder adder_1 (.a(multiplexer_2_out), .b(instruciton_address), .out(adder_1_out));  // open: cin, cout
endmodule

// regfile
module register_file (
  input  [1:0] ri,
  input  [1:0] rj,
  input  [7:0] \input ,
  input  clock,
  input  reset,
  input  write,
  output [7:0] ri_2,
  output [7:0] rj_2
);

  wire demultiplexer_1_out1, demultiplexer_1_out2, demultiplexer_1_out3;
  wire [7:0] register_1_q, register_2_q, register_3_q, register_4_q;

  Demultiplexer #(.select(2)) demultiplexer_1 (
    .out1(demultiplexer_1_out1), .out2(demultiplexer_1_out2), .out3(demultiplexer_1_out3), .in(write),
    .sel(ri));  // open: out0, en
  Multiplexer #(.select(2), .width(8)) multiplexer_1 (
    .in0(register_1_q), .in1(register_2_q), .in2(register_3_q), .in3(register_4_q), .out(ri_2), .sel(ri));  // open: en
  Register register_1 (.Q(register_1_q));  // open: D, en, clk, clr
  Multiplexer #(.select(2), .width(8)) multiplexer_2 (
    .in0(register_1_q), .in1(register_2_q), .in2(register_3_q), .in3(register_4_q), .out(rj_2), .sel(rj));  // open: en
  Register #(.trigger("falling")) register_2 (
    .D(\input ), .en(demultiplexer_1_out1), .Q(register_2_q), .clk(clock), .clr(reset));
  Register #(.trigger("falling")) register_3 (
    .D(\input ), .en(demultiplexer_1_out2), .Q(register_3_q), .clk(clock), .clr(reset));
  Register #(.trigger("falling")) register_4 (
    .D(\input ), .en(demultiplexer_1_out3), .Q(register_4_q), .clk(clock), .clr(reset));
endmodule

// dec
module decoder (
  input  [11:0] instruction,
  output [1:0] op_code,
  output [1:0] \function ,
  output [1:0] rj,
  output [1:0] ri,
  output [7:0] immediate
);


  assign \function  = instruction[11:10];
  assign immediate = instruction[7:0];
  assign op_code = instruction[9:8];
  assign ri = instruction[7:6];
  assign rj = instruction[5:4];
endmodule

// cntrl
module control_unit (
  input  [1:0] op_code,
  input  [1:0] fnction,
  output [1:0] alu_op,
  output branch,
  output jump,
  output stack_push,
  output stack_peak,
  output reg_write,
  output use_immediate,
  output sp_decrease,
  output sp_increase
);

  wire and_7_out, not_1_out;

  and and_1 (branch, ~fnction[1], op_code[0], op_code[1]);  // AND_Gate
  and and_2 (jump, fnction[1], op_code[0], op_code[1]);
  and and_3 (stack_push, ~fnction[0], ~fnction[1], ~op_code[0], op_code[1]);  // AND_Gate
  and and_4 (stack_peak, fnction[0], op_code[1]);
  and and_5 (reg_write, fnction[0], ~fnction[1], ~op_code[0], op_code[1]);  // AND_Gate
  and and_6 (sp_decrease, ~fnction[0], fnction[1], ~op_code[0], op_code[1]);  // AND_Gate
  not not_1 (not_1_out, op_code[1]);
  or or_1 (sp_increase, not_1_out, and_7_out);
  and and_7 (and_7_out, ~fnction[0], ~fnction[1], ~op_code[0], op_code[1]);  // AND_Gate
  and and_8 (use_immediate, ~jump, op_code[0]);  // AND_Gate

  assign alu_op = fnction;
endmodule
